// Logisim project AND_OR_em_NAND.circ as structural Verilog: 1 circuit, main circuit main
module main (
  input  A,
  input  in_2,
  input  AND,
  input  A_2,
  input  in_5,
  input  B,
  input  A_3,
  input  in_8,
  input  OR,
  input  B_2,
  output out_11,
  output x___A_B___A_prime,
  output out_13,
  output out_14,
  output out_15,
  output x___A_prime_B_prime___AB
);

  wire nand_2_out, nand_3_out, nand_4_out;

  not not_1 (out_11, in_2);
  and and_1 (out_13, AND, AND, in_5, in_5);
  or or_1 (out_15, in_8, OR);
  nand nand_1 (x___A_B___A_prime, A, A);
  nand nand_2 (nand_2_out, A_2, B);
  nand nand_3 (nand_3_out, A_3, A_3);
  nand nand_4 (nand_4_out, B_2, B_2);
  nand nand_5 (out_14, nand_2_out, nand_2_out);
  nand nand_6 (x___A_prime_B_prime___AB, nand_3_out, nand_4_out);

  // Notes on the sheet:
  //   NOT
  //   INVERSOR
  //   AND
  //   OR
  //   FEITO EM NAND
  //   A'B
  //   A'
  //   B'
  //   __
  //   x = AB
  //   __
endmodule
