// Logisim project AND_OR_em_NOR.circ as structural Verilog: 1 circuit, main circuit main
module main (
  input  A,
  input  in_2,
  input  OR,
  input  A_2,
  input  OR_2,
  input  B,
  input  AND,
  input  A_3,
  input  in_9,
  input  B_2,
  output out_11,
  output x___A___A___A,
  output out_13,
  output A___B,
  output out_15,
  output x___A_prime_B_prime___AB
);

  wire nor_2_out, nor_3_out, nor_4_out;

  not not_1 (out_11, in_2);
  or or_1 (out_13, OR, OR_2);
  and and_1 (out_15, AND, AND, in_9, in_9);
  nor nor_1 (x___A___A___A, A, A);
  nor nor_2 (nor_2_out, A_2, B);
  nor nor_3 (nor_3_out, A_3, A_3);
  nor nor_4 (nor_4_out, B_2, B_2);
  nor nor_5 (A___B, nor_2_out, nor_2_out);
  nor nor_6 (x___A_prime_B_prime___AB, nor_3_out, nor_4_out);

  // Notes on the sheet:
  //   NOT
  //   INVERSOR
  //   AND
  //   FEITO EM NOR
  //   ____
  //   A + B
  //   A'
  //   B'
  //   _
  //   ____
  //   __
endmodule
