// Logisim project Meio_Subtrator_e_Subtrator_Completo.circ as structural Verilog
module MS___Meio_Subtrator (
  input  A,
  input  B,
  output \Diferença ,
  output Borrow
);

  xor xor_1 (\Diferença , A, B);
  and and_1 (Borrow, ~A, B);  // AND_Gate
endmodule

module SC___Subtrator_Completo (
  input  A,
  input  B,
  input  Borrow_In,
  output Diff,
  output Borrow_Out
);

  wire and_1_out, and_2_out, and_3_out, xor_1_out;

  and and_1 (and_1_out, B, Borrow_In);
  and and_2 (and_2_out, ~A, Borrow_In);  // AND_Gate
  and and_3 (and_3_out, ~A, B);  // AND_Gate
  xor xor_1 (xor_1_out, A, B);
  or or_1 (Borrow_Out, and_1_out, and_2_out, and_3_out);
  xor xor_2 (Diff, xor_1_out, Borrow_In);
endmodule

module teste (
  input  A,
  input  A_2,
  input  B,
  input  B_2,
  input  A0,
  input  B0,
  input  A1,
  input  B1,
  input  A_3,
  input  A_4,
  input  B_3,
  input  B_4,
  output \Diferença ,
  output Diff,
  output Borrow_Out,
  output \Diferença_2 ,
  output Diff_2,
  output S1,
  output S0,
  output Borrow_Out_2
);

  wire and_1_out, and_2_out, and_3_out, and_4_out, and_5_out, and_6_out, and_7_out, and_8_out, and_10_out,
       and_11_out, and_12_out, and_13_out, or_3_out, undriven, undriven_2, xor_3_out, xor_5_out, xor_7_out,
       xor_8_out, xor_9_out;

  xor xor_1 (\Diferença , A, B_2);
  and and_1 (and_1_out, ~A, B_2);  // AND_Gate
  xor xor_2 (\Diferença_2 , A_3, B_4);
  and and_2 (and_2_out, ~A_3, B_4);  // AND_Gate
  xor xor_3 (xor_3_out, A_4, B_3);
  and and_3 (and_3_out, B_3, and_2_out);
  and and_4 (and_4_out, ~A_4, and_2_out);  // AND_Gate
  and and_5 (and_5_out, ~A_4, B_3);  // AND_Gate
  and and_6 (and_6_out, B, and_1_out);
  and and_7 (and_7_out, ~A_2, and_1_out);  // AND_Gate
  and and_8 (and_8_out, ~A_2, B);  // AND_Gate
  xor xor_4 (Diff_2, xor_3_out, and_2_out);
  or or_1 (Borrow_Out_2, and_3_out, and_4_out, and_5_out);
  xor xor_5 (xor_5_out, A_2, B);
  xor xor_6 (Diff, xor_5_out, and_1_out);
  or or_2 (Borrow_Out, and_6_out, and_7_out, and_8_out);
  or or_3 (or_3_out, and_10_out, and_11_out, and_12_out);
  and and_9 (S1, undriven, xor_8_out);
  and and_10 (and_10_out, B1, and_13_out);
  and and_11 (and_11_out, ~A1, and_13_out);  // AND_Gate
  and and_12 (and_12_out, ~A1, B1);  // AND_Gate
  xor xor_7 (xor_7_out, A1, B1);
  xor xor_8 (xor_8_out, xor_7_out, and_13_out);
  and and_13 (and_13_out, ~A0, B0);  // AND_Gate
  and and_14 (S0, xor_9_out, undriven_2);
  xor xor_9 (xor_9_out, A0, B0);
endmodule
