// Logisim project aula_09-06.circ as structural Verilog: 4 circuits, main circuit main
module main (
  input  A,
  input  B,
  output Cn,
  output S
);

  and and_1 (Cn, A, B);
  xor xor_1 (S, A, B);

  // Notes on the sheet:
  //   S = A'B + AB'
  //   Cn+1 = AB
endmodule

module somador (
  input  a3,
  input  b3,
  input  a2,
  input  b2,
  input  a1,
  input  b1,
  input  a0,
  input  b0,
  output r_n_1,
  output r3,
  output r2,
  output r1,
  output r0
);

  wire and_1_out, and_2_out, and_3_out, and_4_out, and_5_out, and_6_out, and_7_out, or_2_out, or_3_out,
       xor_1_out, xor_3_out, xor_6_out;

  and and_1 (and_1_out, b3, or_2_out);
  or or_1 (r_n_1, and_1_out, and_2_out);
  and and_2 (and_2_out, xor_1_out, a3);
  xor xor_1 (xor_1_out, b3, or_2_out);
  xor xor_2 (r3, a3, xor_1_out);
  SC___Somador_Completo sc_somador_completo_1 ();  // open: out_3, in_1, in_2, out_4
  and and_3 (and_3_out, b2, or_3_out);
  or or_2 (or_2_out, and_3_out, and_4_out);
  xor xor_3 (xor_3_out, b2, or_3_out);
  and and_4 (and_4_out, xor_3_out, a2);
  xor xor_4 (r2, a2, xor_3_out);
  SC___Somador_Completo sc_somador_completo_2 ();  // open: out_3, in_1, in_2, out_4
  and and_5 (and_5_out, b1, and_7_out);
  or or_3 (or_3_out, and_5_out, and_6_out);
  and and_6 (and_6_out, xor_6_out, a1);
  xor xor_5 (r1, a1, xor_6_out);
  SC___Somador_Completo sc_somador_completo_3 ();  // open: out_3, in_1, in_2, out_4
  xor xor_6 (xor_6_out, b1, and_7_out);
  and and_7 (and_7_out, a0, b0);
  xor xor_7 (r0, a0, b0);
  MS___Meio_Somador ms_meio_somador_1 ();  // open: in_1, in_2, out_3
endmodule

module SC___Somador_Completo (
  input  in_1,
  input  in_2,
  output out_3,
  output out_4
);

  wire and_1_out, and_2_out, xor_1_out;

  or or_1 (out_3, and_1_out, and_2_out);
  and and_1 (and_1_out, in_2, in_1);
  and and_2 (and_2_out, xor_1_out, in_1);
  xor xor_1 (xor_1_out, in_2, in_1);
  xor xor_2 (out_4, in_1, xor_1_out);
endmodule

module MS___Meio_Somador (
  input  in_1,
  input  in_2,
  output out_3
);

  wire and_1_out;

  and and_1 (and_1_out, in_1, in_2);
  xor xor_1 (out_3, in_1, in_2);
endmodule
