// Logisim project exercicio_05-05-2021.circ as structural Verilog: 1 circuit, main circuit main
module main (
  input  A,
  input  B,
  input  C,
  output x___A_B__A_prime_prime___B_prime_C_prime,
  output x___A_B_C_prime
);

  wire and_1_out, nor_1_out, not_1_out, not_2_out;

  and and_1 (and_1_out, B, C);
  not not_1 (not_1_out, A);
  not not_2 (not_2_out, C);
  nor nor_1 (nor_1_out, not_1_out, and_1_out);
  and and_2 (x___A_B__A_prime_prime___B_prime_C_prime, nor_1_out, A, B);
  and and_3 (x___A_B_C_prime, A, B, not_2_out);

  // Notes on the sheet:
  //   BC
  //   A'' + B' C'
  //   CIRCUITO (a)
  //   CIRCUITO (b)
endmodule
