// Logisim project teorema_booleano_14_15a_15b.circ as structural Verilog: 1 circuit, main circuit main
module main (
  input  x,
  input  x_2,
  input  y,
  input  x_prime,
  input  x_prime_2,
  input  x_prime_3,
  input  y_2,
  input  y_3,
  input  x_3,
  input  x_4,
  input  x_5,
  input  y_4,
  input  y_5,
  input  x_6,
  output out_15,
  output out_16,
  output out_17,
  output out_18,
  output out_19,
  output out_20
);

  wire not_1_out, not_2_out, not_3_out, or_1_out, or_2_out, or_3_out;

  not not_1 (not_1_out, x_3);
  or or_1 (or_1_out, y, x_prime);
  or or_2 (or_2_out, y_3, not_1_out);
  not not_2 (not_2_out, x_5);
  or or_3 (or_3_out, y_5, x_6);
  and and_1 (out_15, x, or_1_out);
  and and_2 (out_17, x_prime_2, or_2_out);
  and and_3 (out_20, not_2_out, or_3_out);
  not not_3 (not_3_out, x_4);
  and and_4 (out_18, x_prime_3, y_2);
  and and_5 (out_19, not_3_out, y_4);

  assign out_16 = x_2;

  // Notes on the sheet:
  //   14
  //   15a
  //   15b
endmodule
