// Logisim project teorema_booleano_16_17.circ as structural Verilog: 1 circuit, main circuit main
module main (
  input  x,
  input  x_2,
  input  y,
  input  y_2,
  input  x_3,
  input  x_4,
  input  y_3,
  input  y_4,
  output out_9,
  output out_10,
  output out_11,
  output out_12
);

  wire and_1_out, and_2_out, not_1_out, not_2_out, not_4_out, not_5_out;

  and and_1 (and_1_out, x, y);
  not not_1 (not_1_out, x_3);
  not not_2 (not_2_out, y_3);
  not not_3 (out_9, and_1_out);
  or or_1 (out_11, not_1_out, not_2_out);
  not not_4 (not_4_out, x_2);
  or or_2 (out_10, not_4_out, not_5_out);
  not not_5 (not_5_out, y_2);
  and and_2 (and_2_out, x_4, y_4);
  not not_6 (out_12, and_2_out);

  // Notes on the sheet:
  //   16
  //   17
endmodule
