// Logisim project teorema_booleano_4.circ as structural Verilog: 1 circuit, main circuit main
module main (
  input  in_1,
  output out_2
);

  not not_1 (in_1, in_1);
  and and_1 (out_2, in_1, in_1);

  // Notes on the sheet:
  //   (4) x . x' = 0
endmodule
