// Logisim project teorema_booleano_5.circ as structural Verilog: 1 circuit, main circuit main
module main (
  input  x,
  input  _0,
  output x_2
);

  or or_1 (x_2, x, _0);

  // Notes on the sheet:
  //   (5) x + 0 = x
endmodule
