// Logisim project teorema_booleano_6.circ as structural Verilog: 1 circuit, main circuit main
module main (
  input  x,
  input  _1,
  output x_2
);

  or or_1 (x_2, x, _1);

  // Notes on the sheet:
  //   (6) x + 1 = 1
endmodule
