// Logisim project teorema_booleano_7.circ as structural Verilog: 1 circuit, main circuit main
module main (
  input  x,
  output x_2
);

  or or_1 (x_2, x, x);

  // Notes on the sheet:
  //   (7) x + x = x
endmodule
