// Logisim project teorema_booleano_8.circ as structural Verilog: 1 circuit, main circuit main
module main (
  input  x,
  output x_2
);

  wire not_1_out;

  not not_1 (not_1_out, x);
  or or_1 (x_2, x, not_1_out);

  // Notes on the sheet:
  //   (8) x + x' = 1
endmodule
