// Logisim project trabalho balança.circ as structural Verilog
module roteiro (
  input  Entrada_do_Peso,
  input  Tara,
  output LED_final
);

  _1 u_1_1 ();
  _2 u_2_1 ();

  assign LED_final = Entrada_do_Peso;
  assign Tara = Entrada_do_Peso;

  // Notes on the sheet:
  //   Separa em duas saídas
  //   Subtrador
  //   Registrador
  //   Quando a tara é pressionada,
  //   o valor que aparece no LED será
  //   Quando a tara não é pressionada
  //   o valor apenas é mostrado no LED
  //   (já que o valor que passa pelo registrador )
  //   (não subtrará o valor final enquanto a tara)
  //   (não for pressionada)
  //   Caso a tara seja pressionada,
  //   o valor será subtraído pelo número registrado previamente,
  //   e caso não haja um número, o mesmo será registrado.
  //   igual a zero, já que o numero do peso será subtraído
  //   pelo valor que está no sistema registrador, e como nada
  //   foi registrado anteriormente, o valor subtrará ele mesmo.
  //   e quando houver um outro número registrado, o peso
  //   será subtraído pelo número registrado.
  //   Em seguida, o valor aparece no LED
endmodule

module Flip_Flop_D (
  input  in_1,
  input  in_2,
  input  in_3,
  input  in_4,
  input  in_5,
  output out_6,
  output out_7,
  output out_8,
  output out_9
);

  D_Flip_Flop d_ff_1 (.clk(in_1), .D(in_2), .Q(out_6));  // open: Qn, preset, en, reset
  D_Flip_Flop d_ff_2 (.clk(in_1), .D(in_3), .Q(out_7));  // open: Qn, preset, en, reset
  D_Flip_Flop d_ff_3 (.clk(in_1), .D(in_4), .Q(out_8));  // open: Qn, preset, en, reset
  D_Flip_Flop d_ff_4 (.clk(in_1), .D(in_5), .Q(out_9));  // open: Qn, preset, en, reset

  // Notes on the sheet:
  //   Flip Flop tipo D
  //   Desvantagem: Uma entrada de dado (?)
  //   Vantagem: Só mudará o resultado quando houver uma mudança de clock
endmodule

module TESTE_1 (
  input  A3,
  input  A2,
  input  A1,
  input  A0,
  input  B3,
  input  B2,
  input  B1,
  input  B0
);

  wire Tara_out;
  wire [3:0] \subcircuito_balança_1_out_10 , \subcircuito_balança_1_out_11 , \subcircuito_balança_1_out_12 ,
       \subcircuito_balança_1_out_13 ;

  Hex_Digit_Display hex_digit_display_1 (.value(\subcircuito_balança_1_out_10 ));  // open: dp
  Hex_Digit_Display hex_digit_display_2 (.value(\subcircuito_balança_1_out_12 ));  // open: dp
  Hex_Digit_Display hex_digit_display_3 (.value(\subcircuito_balança_1_out_11 ));  // open: dp
  Hex_Digit_Display hex_digit_display_4 (.value(\subcircuito_balança_1_out_13 ));  // open: dp
  Button Tara (.out(Tara_out));
  \Subcircuito_Balança  \subcircuito_balança_1  (
    .out_12(\subcircuito_balança_1_out_12 ), .out_13(\subcircuito_balança_1_out_13 ), .Tara(Tara_out),
    .A3(A3), .A2(A2), .A1(A1), .A0(A0), .B3(B3), .B2(B2), .B1(B1), .B0(B0),
    .out_10(\subcircuito_balança_1_out_10 ), .out_11(\subcircuito_balança_1_out_11 ));

  // Notes on the sheet:
  //   Valor Registrado
  //   Peso atual
  //   0000 - 0
  //   0001 - 1
  //   0010 - 2
  //   0011 - 3
  //   0100 - 4
  //   0101 - 5
  //   0110 - 6
  //   0111 - 7
  //   1000 - 8
  //   1001 - 9
endmodule

module \Subcircuito_Balança  (
  input  A3,
  input  A2,
  input  A1,
  input  A0,
  input  B3,
  input  B2,
  input  B1,
  input  B0,
  input  Tara,
  output [3:0] out_10,
  output [3:0] out_11,
  output [3:0] out_12,
  output [3:0] out_13
);

  wire registrador_1_a10, registrador_1_a11, registrador_1_a12, registrador_1_a13, registrador_1_b10,
       registrador_1_b11, registrador_1_b12, registrador_1_b13, subtrator_1_ca3;

  Subtrator subtrator_1 (
    .CA0(out_13[0]), .CA3(subtrator_1_ca3), .A03(A3), .A13(registrador_1_a13), .CA2(out_13[2]), .A02(A2),
    .A12(registrador_1_a12), .CA1(out_13[1]), .A01(A1), .A11(registrador_1_a11), .A00(A0),
    .A10(registrador_1_a10), .B00(B0), .B10(registrador_1_b10), .B03(B3), .B13(registrador_1_b13), .B02(B2),
    .B12(registrador_1_b12), .B01(B1), .B11(registrador_1_b11), .CB3(out_12[3]), .CB2(out_12[2]),
    .CB1(out_12[1]), .CB0(out_12[0]), .Tara(Tara));  // open: Borrow, Borrow_2
  Registrador registrador_1 (
    .Clock(Tara), .A13(registrador_1_a13), .A12(registrador_1_a12), .A11(registrador_1_a11),
    .A10(registrador_1_a10), .B13(registrador_1_b13), .B12(registrador_1_b12), .B11(registrador_1_b11),
    .B10(registrador_1_b10), .A03(A3), .A02(A2), .A01(A1), .A00(A0), .B03(B3), .B02(B2), .B01(B1), .B00(B0));  // open: Clock_2, A03_2, A13_2

  assign out_10 = {A3, A2, A1, A0};
  assign out_11 = {{2{B2}}, B1, B0};
  assign out_13[3] = 1'b1;
endmodule

module Subtrator (
  input  A03,
  input  A13,
  input  A02,
  input  A12,
  input  A01,
  input  A11,
  input  A00,
  input  A10,
  input  B03,
  input  B13,
  input  B02,
  input  B12,
  input  B01,
  input  B11,
  input  B00,
  input  B10,
  input  Tara,
  output Borrow,
  output CA3,
  output CA2,
  output CA1,
  output CA0,
  output Borrow_2,
  output CB3,
  output CB2,
  output CB1,
  output CB0
);

  wire and_1_out, and_2_out, and_3_out, and_5_out, and_6_out, and_7_out, and_9_out, and_10_out, and_11_out,
       and_13_out, and_14_out, and_15_out, and_17_out, and_18_out, and_19_out, and_21_out, and_22_out,
       and_23_out, and_25_out, and_27_out, or_3_out, or_4_out, or_5_out, or_6_out, xor_1_out, xor_2_out,
       xor_3_out, xor_4_out, xor_5_out, xor_6_out, xor_7_out, xor_8_out, xor_9_out, xor_10_out, xor_11_out,
       xor_12_out, xor_13_out, xor_14_out;

  or or_1 (Borrow, and_1_out, and_2_out, and_3_out);
  or or_2 (Borrow_2, and_5_out, and_6_out, and_7_out);
  and and_1 (and_1_out, A13, or_3_out);
  and and_2 (and_2_out, ~A03, or_3_out);  // AND_Gate
  and and_3 (and_3_out, ~A03, A13);  // AND_Gate
  and and_4 (CA3, Tara, xor_2_out);
  xor xor_1 (xor_1_out, A03, A13);
  xor xor_2 (xor_2_out, xor_1_out, or_3_out);
  and and_5 (and_5_out, B13, or_4_out);
  and and_6 (and_6_out, ~B03, or_4_out);  // AND_Gate
  and and_7 (and_7_out, ~B03, B13);  // AND_Gate
  and and_8 (CB3, Tara, xor_4_out);
  xor xor_3 (xor_3_out, B03, B13);
  xor xor_4 (xor_4_out, xor_3_out, or_4_out);
  or or_3 (or_3_out, and_9_out, and_10_out, and_11_out);
  or or_4 (or_4_out, and_13_out, and_14_out, and_15_out);
  and and_9 (and_9_out, A12, or_5_out);
  and and_10 (and_10_out, ~A02, or_5_out);  // AND_Gate
  and and_11 (and_11_out, ~A02, A12);  // AND_Gate
  xor xor_5 (xor_5_out, A02, A12);
  and and_12 (CA2, Tara, xor_6_out);
  xor xor_6 (xor_6_out, xor_5_out, or_5_out);
  and and_13 (and_13_out, B12, or_6_out);
  and and_14 (and_14_out, ~B02, or_6_out);  // AND_Gate
  and and_15 (and_15_out, ~B02, B12);  // AND_Gate
  and and_16 (CB2, Tara, xor_8_out);
  xor xor_7 (xor_7_out, B02, B12);
  xor xor_8 (xor_8_out, xor_7_out, or_6_out);
  or or_5 (or_5_out, and_17_out, and_18_out, and_19_out);
  or or_6 (or_6_out, and_21_out, and_22_out, and_23_out);
  and and_17 (and_17_out, A11, and_25_out);
  and and_18 (and_18_out, ~A01, and_25_out);  // AND_Gate
  and and_19 (and_19_out, ~A01, A11);  // AND_Gate
  and and_20 (CA1, Tara, xor_9_out);
  xor xor_9 (xor_9_out, xor_11_out, and_25_out);
  and and_21 (and_21_out, B11, and_27_out);
  and and_22 (and_22_out, ~B01, and_27_out);  // AND_Gate
  and and_23 (and_23_out, ~B01, B11);  // AND_Gate
  and and_24 (CB1, Tara, xor_10_out);
  xor xor_10 (xor_10_out, xor_12_out, and_27_out);
  xor xor_11 (xor_11_out, A01, A11);
  xor xor_12 (xor_12_out, B01, B11);
  and and_25 (and_25_out, ~A00, A10);  // AND_Gate
  xor xor_13 (xor_13_out, A00, A10);
  and and_26 (CA0, xor_13_out, Tara);
  and and_27 (and_27_out, ~B00, B10);  // AND_Gate
  xor xor_14 (xor_14_out, B00, B10);
  and and_28 (CB0, xor_14_out, Tara);
endmodule

module Registrador (
  input  Clock,
  input  A03,
  input  A02,
  input  A01,
  input  A00,
  input  B03,
  input  B02,
  input  B01,
  input  B00,
  input  A03_2,
  input  Clock_2,
  output A13,
  output A12,
  output A11,
  output A10,
  output B13,
  output B12,
  output B11,
  output B10,
  output A13_2
);

  wire and_1_out, and_2_out, not_2_out, or_1_out, or_2_out;

  D_Flip_Flop d_ff_1 (.clk(Clock), .D(A03), .Q(A13));  // open: Qn, preset, en, reset
  and and_1 (and_1_out, ~A03_2, Clock_2);  // AND_Gate
  and and_2 (and_2_out, Clock_2, A03_2);
  D_Flip_Flop d_ff_2 (.clk(Clock), .D(A02), .Q(A12));  // open: Qn, preset, en, reset
  or or_1 (or_1_out, and_1_out, not_2_out);
  or or_2 (or_2_out, A13_2, and_2_out);
  not not_1 (A13_2, or_1_out);
  not not_2 (not_2_out, or_2_out);
  D_Flip_Flop d_ff_3 (.clk(Clock), .D(A01), .Q(A11));  // open: Qn, preset, en, reset
  D_Flip_Flop d_ff_4 (.clk(Clock), .D(A00), .Q(A10));  // open: Qn, preset, en, reset
  D_Flip_Flop d_ff_5 (.clk(Clock), .D(B03), .Q(B13));  // open: Qn, preset, en, reset
  D_Flip_Flop d_ff_6 (.clk(Clock), .D(B02), .Q(B12));  // open: Qn, preset, en, reset
  D_Flip_Flop d_ff_7 (.clk(Clock), .D(B01), .Q(B11));  // open: Qn, preset, en, reset
  D_Flip_Flop d_ff_8 (.clk(Clock), .D(B00), .Q(B10));  // open: Qn, preset, en, reset
endmodule

module subtrator_dnv (
  input  A13,
  input  A03,
  input  A12,
  input  A02,
  input  A11,
  input  A01,
  input  A10,
  input  A00,
  input  Tara,
  input  B13,
  input  B03,
  input  B12,
  input  B02,
  input  B11,
  input  B01,
  input  B10,
  input  B00,
  input  A00_2,
  input  B00_2,
  input  A03_2,
  input  B03_2,
  input  A02_2,
  input  B02_2,
  input  A01_2,
  input  B01_2,
  input  A10_2,
  input  B10_2,
  input  A13_2,
  input  B13_2,
  input  A12_2,
  input  B12_2,
  input  A11_2,
  input  B11_2,
  input  B10_3,
  input  B00_3,
  input  Tara_2,
  output Borrow,
  output C03,
  output C02,
  output C01,
  output C00,
  output CA3,
  output CA2,
  output CA1,
  output CA0,
  output CB3,
  output CB2,
  output CB1,
  output CB0,
  output Borrow_2,
  output C13,
  output C12,
  output C11,
  output C10,
  output CB0_2
);

  wire and_1_out, and_5_out, and_6_out, and_7_out, and_8_out, and_9_out, and_10_out, and_13_out, and_14_out,
       and_15_out, and_16_out, and_17_out, and_18_out, and_21_out, and_22_out, and_23_out, and_24_out,
       and_25_out, and_26_out, and_27_out, and_29_out, or_3_out, or_4_out, or_5_out, or_6_out, xor_1_out,
       xor_2_out, xor_3_out, xor_4_out, xor_5_out, xor_6_out, xor_7_out, xor_8_out, xor_9_out, xor_10_out,
       xor_11_out, xor_12_out, xor_13_out, xor_14_out, xor_15_out;

  and and_1 (and_1_out, ~B10_3, B00_3);  // AND_Gate
  and and_2 (CB0_2, xor_1_out, Tara_2);
  xor xor_1 (xor_1_out, B10_3, B00_3);
  or or_1 (Borrow, and_5_out, and_6_out, and_7_out);
  and and_3 (C03, xor_2_out, xor_2_out);
  xor xor_2 (xor_2_out, xor_4_out, or_3_out);
  or or_2 (Borrow_2, and_8_out, and_9_out, and_10_out);
  and and_4 (C13, xor_3_out, xor_3_out);
  xor xor_3 (xor_3_out, xor_5_out, or_4_out);
  and and_5 (and_5_out, B03_2, or_3_out);
  and and_6 (and_6_out, ~A03_2, or_3_out);  // AND_Gate
  and and_7 (and_7_out, ~A03_2, B03_2);  // AND_Gate
  xor xor_4 (xor_4_out, A03_2, B03_2);
  and and_8 (and_8_out, B13_2, or_4_out);
  and and_9 (and_9_out, ~A13_2, or_4_out);  // AND_Gate
  and and_10 (and_10_out, ~A13_2, B13_2);  // AND_Gate
  xor xor_5 (xor_5_out, A13_2, B13_2);
  or or_3 (or_3_out, and_13_out, and_14_out, and_15_out);
  and and_11 (C02, xor_7_out, xor_7_out);
  or or_4 (or_4_out, and_16_out, and_17_out, and_18_out);
  and and_12 (C12, xor_9_out, xor_9_out);
  and and_13 (and_13_out, B02_2, or_5_out);
  and and_14 (and_14_out, ~A02_2, or_5_out);  // AND_Gate
  and and_15 (and_15_out, ~A02_2, B02_2);  // AND_Gate
  xor xor_6 (xor_6_out, A02_2, B02_2);
  xor xor_7 (xor_7_out, xor_6_out, or_5_out);
  and and_16 (and_16_out, B12_2, or_6_out);
  and and_17 (and_17_out, ~A12_2, or_6_out);  // AND_Gate
  and and_18 (and_18_out, ~A12_2, B12_2);  // AND_Gate
  xor xor_8 (xor_8_out, A12_2, B12_2);
  xor xor_9 (xor_9_out, xor_8_out, or_6_out);
  or or_5 (or_5_out, and_21_out, and_22_out, and_23_out);
  and and_19 (C01, xor_11_out, xor_11_out);
  or or_6 (or_6_out, and_24_out, and_25_out, and_26_out);
  and and_20 (C11, xor_13_out, xor_13_out);
  and and_21 (and_21_out, B01_2, and_27_out);
  and and_22 (and_22_out, ~A01_2, and_27_out);  // AND_Gate
  and and_23 (and_23_out, ~A01_2, B01_2);  // AND_Gate
  xor xor_10 (xor_10_out, A01_2, B01_2);
  xor xor_11 (xor_11_out, xor_10_out, and_27_out);
  and and_24 (and_24_out, B11_2, and_29_out);
  and and_25 (and_25_out, ~A11_2, and_29_out);  // AND_Gate
  and and_26 (and_26_out, ~A11_2, B11_2);  // AND_Gate
  xor xor_12 (xor_12_out, A11_2, B11_2);
  xor xor_13 (xor_13_out, xor_12_out, and_29_out);
  and and_27 (and_27_out, ~A00_2, B00_2);  // AND_Gate
  and and_28 (C00, xor_14_out, xor_14_out);
  and and_29 (and_29_out, ~A10_2, B10_2);  // AND_Gate
  and and_30 (C10, xor_15_out, xor_15_out);
  xor xor_14 (xor_14_out, A00_2, B00_2);
  xor xor_15 (xor_15_out, A10_2, B10_2);
endmodule
