// Logisim project trabalho_2.circ as structural Verilog: 9 circuits, main circuit main
module main (
  input  in_1,
  input  in_2,
  input  in_3,
  input  in_4,
  input  in_5,
  input  in_6,
  input  A,
  input  SEL,
  input  B,
  input  A_2,
  input  SEL_2,
  output out_12,
  output out_13,
  output out_14,
  output out_15,
  output out_16,
  output out_17
);

  wire and_1_out, and_2_out, not_1_out, not_2_out;

  not not_1 (not_1_out, SEL);
  Multiplexer multiplexer_1 (.in0(in_1), .in1(in_6), .out(out_14));  // open: sel, en
  and and_1 (and_1_out, A, not_1_out);
  and and_2 (and_2_out, SEL, B);
  and and_3 (out_16, A_2, not_2_out);
  not not_2 (not_2_out, SEL_2);
  and and_4 (out_17, A_2, SEL_2);
  or or_1 (out_15, and_1_out, and_2_out);
  Multiplexer multiplexer_2 ();  // open: in0, in1, out, sel, en
  Demultiplexer demultiplexer_1 ();  // open: out0, out1, in, sel, en
  and and_5 (out_13, in_2, in_4);

  assign in_5 = in_4;
  assign out_12 = in_1;

  // Notes on the sheet:
  //   MUX2:1
  //   DEMUX2:1
endmodule

module mux_4_1_com_1_bit (
  input  A,
  input  B,
  input  C,
  input  D,
  input  SEL_1,
  input  SEL_0,
  input  A_2,
  input  B_2,
  input  C_2,
  input  D_2,
  input  SEL_1_2,
  input  SEL_0_2,
  output out_13,
  output out_14
);

  wire _00_out, _01_out, _10_out, _11_out, mux_4_1_1b_1_out_4, mux_4_1_1b_2_out_4, not_1_out, not_2_out;

  mux_4_1_1b mux_4_1_1b_1 (.A(A), .SEL(SEL_0), .B(B), .out_4(mux_4_1_1b_1_out_4));
  mux_4_1_1b mux_4_1_1b_2 (.A(C), .SEL(SEL_0), .B(D), .out_4(mux_4_1_1b_2_out_4));
  not not_1 (not_1_out, SEL_1_2);
  mux_4_1_1b mux_4_1_1b_3 (.A(mux_4_1_1b_1_out_4), .SEL(SEL_1), .B(mux_4_1_1b_2_out_4), .out_4(out_13));
  not not_2 (not_2_out, SEL_0_2);
  and _00 (_00_out, A_2, not_1_out, not_2_out);
  and _01 (_01_out, B_2, not_1_out, SEL_0_2);
  and _10 (_10_out, C_2, SEL_1_2, not_2_out);
  and _11 (_11_out, D_2, SEL_1_2, SEL_0_2);
  or or_1 (out_14, _00_out, _01_out, _10_out, _11_out);

  // Notes on the sheet:
  //   v1
  //   v2
endmodule

module demux_1_4_com_1_bit (
  input  A,
  input  SEL_1,
  input  SEL_0,
  input  A_2,
  input  SEL_1_2,
  input  SEL_0_2,
  output S0,
  output S1,
  output S2,
  output S3,
  output out_11,
  output out_12,
  output out_13,
  output out_14
);

  wire demux_4_1_1b_1_out_3, demux_4_1_1b_1_out_4, not_1_out, not_2_out;

  not not_1 (not_1_out, SEL_1_2);
  demux_4_1_1b demux_4_1_1b_1 (.A(A), .SEL(SEL_0), .out_3(demux_4_1_1b_1_out_3), .out_4(demux_4_1_1b_1_out_4));
  and _00 (out_11, A_2, not_1_out, not_2_out);
  and _01 (out_12, A_2, not_1_out, SEL_0_2);
  and _10 (out_13, A_2, SEL_1_2, not_2_out);
  and _11 (out_14, A_2, SEL_1_2, SEL_0_2);
  not not_2 (not_2_out, SEL_0_2);
  demux_4_1_1b demux_4_1_1b_2 (.A(demux_4_1_1b_1_out_3), .SEL(SEL_1), .out_3(S0), .out_4(S1));
  demux_4_1_1b demux_4_1_1b_3 (.A(demux_4_1_1b_1_out_4), .SEL(SEL_1), .out_3(S2), .out_4(S3));

  // Notes on the sheet:
  //   v1
  //   v2
endmodule

module mux_4_1_1b (
  input  A,
  input  SEL,
  input  B,
  output out_4
);

  wire and_1_out, and_2_out, not_1_out;

  not not_1 (not_1_out, SEL);
  and and_1 (and_1_out, A, not_1_out);
  or or_1 (out_4, and_1_out, and_2_out);
  and and_2 (and_2_out, SEL, B);
endmodule

module demux_4_1_1b (
  input  A,
  input  SEL,
  output out_3,
  output out_4
);

  wire not_1_out;

  and and_1 (out_3, A, not_1_out);
  not not_1 (not_1_out, SEL);
  and and_2 (out_4, A, SEL);
endmodule

module mux_2_1_com_4_bits (
  input  A3,
  input  A2,
  input  A1,
  input  A0,
  input  SEL,
  input  B3,
  input  B2,
  input  B1,
  input  B0,
  input  A,
  input  SEL_2,
  input  B,
  output out_13,
  output out_14
);

  wire and_1_out, and_2_out, and_3_out, and_4_out, not_1_out, not_2_out;

  not not_1 (not_1_out, SEL);
  not not_2 (not_2_out, SEL_2);
  and and_1 (and_1_out, A3, A2, A1, A0, not_1_out);
  and and_2 (and_2_out, SEL, B3, B2, B1, B0);
  and and_3 (and_3_out, A, not_2_out);
  or or_1 (out_14, and_3_out, and_4_out);
  and and_4 (and_4_out, SEL_2, B);
  or or_2 (out_13, and_1_out, and_2_out);
endmodule

module demux_1_2_com_4_bits (
  input  in_1,
  input  in_2,
  input  in_3,
  input  in_4,
  input  in_5,
  input  A,
  input  SEL,
  output out_8,
  output out_9,
  output out_10,
  output out_11
);

  wire and_1_out, and_2_out, and_3_out, and_4_out, not_1_out, not_2_out, not_3_out;

  not not_1 (not_1_out, in_5);
  not not_2 (not_2_out, in_5);
  and and_1 (and_1_out, in_1, in_2, in_3, in_4, not_1_out);
  and and_2 (and_2_out, in_1, in_2, in_3, in_4, in_5);
  and and_3 (and_3_out, in_1, in_2, in_3, in_4, not_2_out);
  and and_4 (and_4_out, in_1, in_2, in_3, in_4, in_5);
  and and_5 (out_10, A, not_3_out);
  not not_3 (not_3_out, SEL);
  and and_6 (out_11, A, SEL);
  and and_7 (out_8, and_1_out, and_3_out);
  and and_8 (out_9, and_2_out, in_5, and_4_out);
endmodule

module mux_2_1_4__bits (
  input  A,
  input  SEL,
  input  B,
  output out_4
);

  wire and_1_out, and_2_out, not_1_out;

  not not_1 (not_1_out, SEL);
  and and_1 (and_1_out, A, not_1_out);
  or or_1 (out_4, and_1_out, and_2_out);
  and and_2 (and_2_out, SEL, B);
endmodule

module demux_1_2_4_bits (
  input  A,
  input  SEL,
  output out_3,
  output out_4
);

  wire not_1_out;

  and and_1 (out_3, A, not_1_out);
  not not_1 (not_1_out, SEL);
  and and_2 (out_4, A, SEL);
endmodule
