// Logisim project trabalho_circuitos.circ as structural Verilog: 17 circuits, main circuit TRABALHO PARTE 1
module TRABALHO_PARTE_1 (
  input  D0,
  input  D1,
  input  D2,
  input  D3
);

  wire controlador_1_out_5, controlador_1_out_6, controlador_1_out_7, controlador_1_out_8,
       controlador_1_out_9, controlador_1_out_10, controlador_1_out_11, controlador_minimizado_1_out_5,
       controlador_minimizado_1_out_6, controlador_minimizado_1_out_7, controlador_minimizado_1_out_8,
       controlador_minimizado_1_out_9, controlador_minimizado_1_out_10, controlador_minimizado_1_out_11;

  Controlador controlador_1 (
    .D3(D3), .D2(D2), .D1(D1), .D0(D0), .out_5(controlador_1_out_5), .out_6(controlador_1_out_6),
    .out_7(controlador_1_out_7), .out_8(controlador_1_out_8), .out_9(controlador_1_out_9),
    .out_10(controlador_1_out_10), .out_11(controlador_1_out_11));
  Controlador_minimizado controlador_minimizado_1 (
    .D3(D3), .D2(D2), .D1(D1), .D0(D0), .out_5(controlador_minimizado_1_out_5),
    .out_6(controlador_minimizado_1_out_6), .out_7(controlador_minimizado_1_out_7),
    .out_8(controlador_minimizado_1_out_8), .out_9(controlador_minimizado_1_out_9),
    .out_10(controlador_minimizado_1_out_10), .out_11(controlador_minimizado_1_out_11));
  _7_Segment_Display u_7_segment_display_1 (
    .g(controlador_1_out_11), .f(controlador_1_out_10), .a(controlador_1_out_5), .b(controlador_1_out_6),
    .e(controlador_1_out_9), .d(controlador_1_out_8), .c(controlador_1_out_7));  // open: dp
  _7_Segment_Display u_7_segment_display_2 (
    .g(controlador_minimizado_1_out_11), .f(controlador_minimizado_1_out_10),
    .a(controlador_minimizado_1_out_5), .b(controlador_minimizado_1_out_6),
    .e(controlador_minimizado_1_out_9), .d(controlador_minimizado_1_out_8), .c(controlador_minimizado_1_out_7));  // open: dp
endmodule

module filamento_a (
  input  D3,
  input  D2,
  input  D1,
  input  D0,
  output out_5
);

  wire _0000_out, _0010_out, _0100_out, _0101_out, _0110_out, _1011_out, _1100_out, _1101_out, not_1_out,
       not_2_out, not_3_out, not_4_out;

  not not_1 (not_1_out, D3);
  not not_2 (not_2_out, D1);
  not not_3 (not_3_out, D2);
  not not_4 (not_4_out, D0);
  and _0000 (_0000_out, not_1_out, not_3_out, not_2_out, not_4_out);
  and _0010 (_0010_out, not_1_out, not_3_out, D1, not_4_out);
  and _0100 (_0100_out, not_1_out, D2, not_2_out, not_4_out);
  and _0101 (_0101_out, not_1_out, D2, not_2_out, D0);
  and _0110 (_0110_out, not_1_out, D2, D1, not_4_out);
  and _1011 (_1011_out, D3, not_3_out, D1, D0);
  and _1100 (_1100_out, D3, D2, not_2_out, not_4_out);
  and _1101 (_1101_out, D3, D2, not_2_out, D0);
  or or_1 (out_5, _0000_out, _0010_out, _0100_out, _0101_out, _0110_out, _1011_out, _1100_out, _1101_out);
endmodule

module filamento_b (
  input  D3,
  input  D2,
  input  D1,
  input  D0,
  output out_5
);

  wire _0000_out, _0011_out, _0111_out, _1001_out, _1011_out, _1100_out, _1101_out, _1110_out, _1111_out,
       not_1_out, not_2_out, not_3_out, not_4_out;

  not not_1 (not_1_out, D3);
  not not_2 (not_2_out, D2);
  not not_3 (not_3_out, D1);
  not not_4 (not_4_out, D0);
  and _0000 (_0000_out, not_1_out, not_2_out, not_3_out, not_4_out);
  and _0011 (_0011_out, not_1_out, not_2_out, D1, D0);
  and _0111 (_0111_out, not_1_out, D2, D1, D0);
  and _1001 (_1001_out, D3, not_2_out, not_3_out, D0);
  and _1011 (_1011_out, D3, not_2_out, D1, D0);
  and _1100 (_1100_out, D3, D2, not_3_out, not_4_out);
  and _1101 (_1101_out, D3, D2, not_3_out, D0);
  and _1110 (_1110_out, D3, D2, D1, not_4_out);
  and _1111 (_1111_out, D3, D2, D1, D0);
  or or_1 (out_5, _0000_out, _0011_out, _0111_out, _1001_out, _1011_out, _1100_out, _1101_out, _1110_out, _1111_out);
endmodule

module filamento_c (
  input  D3,
  input  D2,
  input  D1,
  input  D0,
  output out_5
);

  wire _0000_out, _0001_out, _0011_out, _0110_out, _0111_out, _1001_out, _1011_out, _1100_out, _1110_out,
       _1111_out, not_1_out, not_2_out, not_3_out, not_4_out;

  not not_1 (not_1_out, D3);
  not not_2 (not_2_out, D2);
  not not_3 (not_3_out, D1);
  not not_4 (not_4_out, D0);
  and _0000 (_0000_out, not_1_out, not_2_out, not_3_out, not_4_out);
  and _0001 (_0001_out, not_1_out, not_2_out, not_3_out, D0);
  and _0011 (_0011_out, not_1_out, not_2_out, D1, D0);
  and _0110 (_0110_out, not_1_out, D2, D1, not_4_out);
  and _0111 (_0111_out, not_1_out, D2, D1, D0);
  and _1001 (_1001_out, D3, not_2_out, not_3_out, D0);
  and _1011 (_1011_out, D3, not_2_out, D1, D0);
  and _1100 (_1100_out, D3, D2, not_3_out, not_4_out);
  and _1110 (_1110_out, D3, D2, D1, not_4_out);
  and _1111 (_1111_out, D3, D2, D1, D0);
  or or_1 (out_5, _0000_out, _0001_out, _0011_out, _0110_out, _0111_out, _1001_out, _1011_out, _1100_out, _1110_out, _1111_out);
endmodule

module filamento_d (
  input  D3,
  input  D2,
  input  D1,
  input  D0,
  output out_5
);

  wire _0001_out, _0010_out, _0011_out, _0100_out, _0110_out, _1001_out, _1010_out, _1100_out, _1110_out,
       _1111_out, not_1_out, not_2_out, not_3_out, not_4_out;

  not not_1 (not_1_out, D3);
  not not_2 (not_2_out, D2);
  not not_3 (not_3_out, D1);
  not not_4 (not_4_out, D0);
  and _0001 (_0001_out, not_1_out, not_2_out, not_3_out, D0);
  and _0010 (_0010_out, not_1_out, not_2_out, D1, not_4_out);
  and _0011 (_0011_out, not_1_out, not_2_out, D1, D0);
  and _0100 (_0100_out, not_1_out, D2, not_3_out, not_4_out);
  and _0110 (_0110_out, not_1_out, D2, D1, not_4_out);
  and _1001 (_1001_out, D3, not_2_out, not_3_out, D0);
  and _1010 (_1010_out, D3, not_2_out, D1, not_4_out);
  and _1100 (_1100_out, D3, D2, not_3_out, not_4_out);
  and _1110 (_1110_out, D3, D2, D1, not_4_out);
  and _1111 (_1111_out, D3, D2, D1, D0);
  or or_1 (out_5, _0001_out, _0010_out, _0011_out, _0100_out, _0110_out, _1001_out, _1010_out, _1100_out, _1110_out, _1111_out);
endmodule

module filamento_e (
  input  D3,
  input  D2,
  input  D1,
  input  D0,
  output out_5
);

  wire _0000_out, _0001_out, _0010_out, _0011_out, _0100_out, _0101_out, _0110_out, _0111_out, _1000_out,
       _1001_out, _1010_out, _1011_out, _1100_out, _1101_out, _1110_out, not_1_out, not_2_out, not_3_out,
       not_4_out;

  not not_1 (not_1_out, D3);
  not not_2 (not_2_out, D1);
  not not_3 (not_3_out, D2);
  not not_4 (not_4_out, D0);
  and _0000 (_0000_out, not_1_out, not_3_out, not_2_out, not_4_out);
  and _0001 (_0001_out, not_1_out, not_3_out, not_2_out, D0);
  and _0010 (_0010_out, not_1_out, not_3_out, D1, not_4_out);
  and _0011 (_0011_out, not_1_out, not_3_out, D1, D0);
  and _0100 (_0100_out, not_1_out, D2, not_2_out, not_4_out);
  and _0101 (_0101_out, not_1_out, D2, not_2_out, D0);
  and _0110 (_0110_out, not_1_out, D2, D1, not_4_out);
  and _0111 (_0111_out, not_1_out, D2, D1, D0);
  and _1000 (_1000_out, D3, not_3_out, not_2_out, not_4_out);
  and _1001 (_1001_out, D3, not_3_out, not_2_out, D0);
  and _1010 (_1010_out, D3, not_3_out, D1, not_4_out);
  and _1011 (_1011_out, D3, not_3_out, D1, D0);
  and _1100 (_1100_out, D3, D2, not_2_out, not_4_out);
  and _1101 (_1101_out, D3, D2, not_2_out, D0);
  and _1110 (_1110_out, D3, D2, D1, not_4_out);
  or or_1 (out_5, _0000_out, _0001_out, _0010_out, _0011_out, _0100_out, _0101_out, _0110_out, _0111_out, _1000_out, _1001_out, _1010_out, _1011_out, _1100_out, _1101_out, _1110_out);
endmodule

module filamento_f (
  input  D3,
  input  D2,
  input  D1,
  input  D0,
  output out_5
);

  wire _0000_out, _0001_out, _0010_out, _0100_out, _0101_out, _0110_out, _0111_out, _1000_out, _1010_out,
       _1011_out, _1100_out, _1101_out, _1110_out, _1111_out, not_1_out, not_2_out, not_3_out, not_4_out;

  not not_1 (not_1_out, D3);
  not not_2 (not_2_out, D2);
  not not_3 (not_3_out, D1);
  not not_4 (not_4_out, D0);
  and _0000 (_0000_out, not_1_out, not_2_out, not_3_out, not_4_out);
  and _0001 (_0001_out, not_1_out, not_2_out, not_3_out, D0);
  and _0010 (_0010_out, not_1_out, not_2_out, D1, not_4_out);
  and _0100 (_0100_out, not_1_out, D2, not_3_out, not_4_out);
  and _0101 (_0101_out, not_1_out, D2, not_3_out, D0);
  and _0110 (_0110_out, not_1_out, D2, D1, not_4_out);
  and _0111 (_0111_out, not_1_out, D2, D1, D0);
  and _1000 (_1000_out, D3, not_2_out, not_3_out, not_4_out);
  and _1010 (_1010_out, D3, not_2_out, D1, not_4_out);
  and _1011 (_1011_out, D3, not_2_out, D1, D0);
  and _1100 (_1100_out, D3, D2, not_3_out, not_4_out);
  and _1101 (_1101_out, D3, D2, not_3_out, D0);
  and _1110 (_1110_out, D3, D2, D1, not_4_out);
  and _1111 (_1111_out, D3, D2, D1, D0);
  or or_1 (out_5, _0000_out, _0001_out, _0010_out, _0100_out, _0101_out, _0110_out, _0111_out, _1000_out, _1010_out, _1011_out, _1100_out, _1101_out, _1110_out, _1111_out);
endmodule

module filamento_g (
  input  D3,
  input  D2,
  input  D1,
  input  D0,
  output out_5
);

  wire _0000_out, _0001_out, _0011_out, _0100_out, _0101_out, _0111_out, _1101_out, _1111_out, not_1_out,
       not_2_out, not_3_out, not_4_out;

  not not_1 (not_1_out, D3);
  not not_2 (not_2_out, D1);
  not not_3 (not_3_out, D2);
  not not_4 (not_4_out, D0);
  and _0000 (_0000_out, not_1_out, not_3_out, not_2_out, not_4_out);
  and _0001 (_0001_out, not_1_out, not_3_out, not_2_out, D0);
  and _0011 (_0011_out, not_1_out, not_3_out, D1, D0);
  and _0100 (_0100_out, not_1_out, D2, not_2_out, not_4_out);
  and _0101 (_0101_out, not_1_out, D2, not_2_out, D0);
  and _0111 (_0111_out, not_1_out, D2, D1, D0);
  and _1101 (_1101_out, D3, D2, not_2_out, D0);
  and _1111 (_1111_out, D3, D2, D1, D0);
  or or_1 (out_5, _0000_out, _0001_out, _0011_out, _0100_out, _0101_out, _0111_out, _1101_out, _1111_out);
endmodule

module Controlador (
  input  D3,
  input  D2,
  input  D1,
  input  D0,
  output out_5,
  output out_6,
  output out_7,
  output out_8,
  output out_9,
  output out_10,
  output out_11
);

  filamento_a filamento_a_1 (.D3(D3), .D2(D2), .D1(D1), .D0(D0), .out_5(out_5));
  filamento_b filamento_b_1 (.D3(D3), .D2(D2), .D1(D1), .D0(D0), .out_5(out_6));
  filamento_c filamento_c_1 (.D3(D3), .D2(D2), .D1(D1), .D0(D0), .out_5(out_7));
  filamento_d filamento_d_1 (.D3(D3), .D2(D2), .D1(D1), .D0(D0), .out_5(out_8));
  filamento_e filamento_e_1 (.D3(D0), .D2(D1), .D1(D2), .D0(D3), .out_5(out_9));
  filamento_f filamento_f_1 (.D3(D3), .D2(D2), .D1(D1), .D0(D0), .out_5(out_10));
  filamento_g filamento_g_1 (.D3(D3), .D2(D2), .D1(D1), .D0(D0), .out_5(out_11));
endmodule

module filamento_a_minimizado (
  input  D3,
  input  D2,
  input  D1,
  input  D0,
  output out_5
);

  wire and_1_out, and_2_out, and_3_out, not_1_out, not_2_out, not_3_out, not_4_out;

  not not_1 (not_1_out, D3);
  not not_2 (not_2_out, D1);
  not not_3 (not_3_out, D2);
  not not_4 (not_4_out, D0);
  and and_1 (and_1_out, D2, not_2_out);
  and and_2 (and_2_out, not_1_out, not_4_out);
  and and_3 (and_3_out, D3, not_3_out, D1, D0);
  or or_1 (out_5, and_1_out, and_2_out, and_3_out);
endmodule

module filamento_b_minimizado (
  input  D3,
  input  D2,
  input  D1,
  input  D0,
  output out_5
);

  wire and_1_out, and_2_out, and_3_out, and_4_out, not_1_out, not_2_out, not_3_out, not_4_out;

  not not_1 (not_1_out, D3);
  not not_2 (not_2_out, D1);
  not not_3 (not_3_out, D2);
  not not_4 (not_4_out, D0);
  and and_1 (and_1_out, not_1_out, not_3_out, not_2_out, not_4_out);
  and and_2 (and_2_out, D1, D0);
  and and_3 (and_3_out, D3, D0);
  and and_4 (and_4_out, D3, D2);
  or or_1 (out_5, and_1_out, and_2_out, and_3_out, and_4_out);
endmodule

module filamento_c_minimizado (
  input  D3,
  input  D2,
  input  D1,
  input  D0,
  output out_5
);

  wire and_1_out, and_2_out, and_3_out, and_4_out, not_1_out, not_2_out, not_3_out, not_4_out;

  not not_1 (not_1_out, D3);
  not not_2 (not_2_out, D1);
  not not_3 (not_3_out, D2);
  not not_4 (not_4_out, D0);
  and and_1 (and_1_out, D3, D2, not_4_out);
  and and_2 (and_2_out, not_1_out, not_3_out, not_2_out);
  and and_3 (and_3_out, not_3_out, D0);
  and and_4 (and_4_out, D2, D1);
  or or_1 (out_5, and_1_out, and_2_out, and_3_out, and_4_out);
endmodule

module filamento_d_minimizado (
  input  D3,
  input  D2,
  input  D1,
  input  D0,
  output out_5
);

  wire and_1_out, and_2_out, and_3_out, and_4_out, and_5_out, not_1_out, not_2_out, not_3_out, not_4_out;

  not not_1 (not_1_out, D3);
  not not_2 (not_2_out, D2);
  not not_3 (not_3_out, D1);
  not not_4 (not_4_out, D0);
  and and_1 (and_1_out, D1, not_4_out);
  and and_2 (and_2_out, not_1_out, not_2_out, D0);
  and and_3 (and_3_out, D2, not_4_out);
  and and_4 (and_4_out, D3, D2, D1);
  and and_5 (and_5_out, not_2_out, not_3_out, D0);
  or or_1 (out_5, and_1_out, and_2_out, and_3_out, and_4_out, and_5_out);
endmodule

module filamento_e_minimizado (
  input  D3,
  input  D2,
  input  D1,
  input  D0,
  output out_5
);

  wire not_1_out, not_2_out, not_3_out, not_4_out;

  not not_1 (not_1_out, D3);
  not not_2 (not_2_out, D2);
  not not_3 (not_3_out, D1);
  not not_4 (not_4_out, D0);
  or or_1 (out_5, not_1_out, not_2_out, not_3_out, not_4_out);
endmodule

module filamento_f_minimizado (
  input  D3,
  input  D2,
  input  D1,
  input  D0,
  output out_5
);

  wire and_1_out, and_2_out, not_1_out, not_2_out, not_3_out, not_4_out;

  not not_1 (not_1_out, D3);
  not not_2 (not_2_out, D2);
  not not_3 (not_3_out, D1);
  not not_4 (not_4_out, D0);
  and and_1 (and_1_out, not_1_out, not_3_out);
  and and_2 (and_2_out, D3, D1);
  or or_1 (out_5, and_1_out, and_2_out, D2, not_4_out);
endmodule

module filamento_g_minimizado (
  input  D3,
  input  D2,
  input  D1,
  input  D0,
  output out_5
);

  wire and_1_out, and_2_out, and_3_out, not_1_out, not_2_out, not_3_out, not_4_out;

  not not_1 (not_1_out, D3);
  not not_2 (not_2_out, D1);
  not not_3 (not_3_out, D2);
  not not_4 (not_4_out, D0);
  and and_1 (and_1_out, not_1_out, not_2_out);
  and and_2 (and_2_out, not_1_out, D0);
  and and_3 (and_3_out, D2, D0);
  or or_1 (out_5, and_1_out, and_2_out, and_3_out);
endmodule

module Controlador_minimizado (
  input  D3,
  input  D2,
  input  D1,
  input  D0,
  output out_5,
  output out_6,
  output out_7,
  output out_8,
  output out_9,
  output out_10,
  output out_11
);

  filamento_a_minimizado filamento_a_minimizado_1 (.out_5(out_5), .D3(D3), .D2(D2), .D1(D1), .D0(D0));
  filamento_b_minimizado filamento_b_minimizado_1 (.out_5(out_6), .D3(D3), .D2(D2), .D1(D1), .D0(D0));
  filamento_c_minimizado filamento_c_minimizado_1 (.out_5(out_7), .D3(D3), .D2(D2), .D1(D1), .D0(D0));
  filamento_d_minimizado filamento_d_minimizado_1 (.out_5(out_8), .D3(D3), .D2(D2), .D1(D1), .D0(D0));
  filamento_e_minimizado filamento_e_minimizado_1 (.out_5(out_9), .D3(D3), .D2(D2), .D1(D1), .D0(D0));
  filamento_f_minimizado filamento_f_minimizado_1 (.out_5(out_10), .D3(D3), .D2(D2), .D1(D1), .D0(D0));
  filamento_g_minimizado filamento_g_minimizado_1 (.out_5(out_11), .D3(D3), .D2(D2), .D1(D1), .D0(D0));
endmodule
