// Logisim project trabalho_ula.circ as structural Verilog
module \unidade_lógica_de_4_bits  (
  input  A3,
  input  A2,
  input  A1,
  input  A0,
  input  B3,
  input  B2,
  input  B1,
  input  B0,
  input  S1,
  input  S0,
  output F3,
  output F2,
  output F1,
  output F0
);

  wire and_1_out, and_2_out, and_3_out, and_4_out, multiplexer_1_out, multiplexer_2_out, multiplexer_3_out,
       multiplexer_4_out, multiplexer_5_out, multiplexer_6_out, multiplexer_7_out, multiplexer_8_out,
       not_1_out, not_2_out, not_3_out, not_4_out, or_1_out, or_2_out, or_3_out, or_4_out, xor_1_out,
       xor_2_out, xor_3_out, xor_4_out;

  and and_1 (and_1_out, B0, A0);
  or or_1 (or_1_out, B0, A0);
  not not_1 (not_1_out, A0);
  xor xor_1 (xor_1_out, B0, A0);
  and and_2 (and_2_out, B1, A1);
  or or_2 (or_2_out, B1, A1);
  not not_2 (not_2_out, A1);
  xor xor_2 (xor_2_out, B1, A1);
  and and_3 (and_3_out, B2, A2);
  or or_3 (or_3_out, B2, A2);
  not not_3 (not_3_out, A2);
  xor xor_3 (xor_3_out, B2, A2);
  and and_4 (and_4_out, B3, A3);
  or or_4 (or_4_out, B3, A3);
  not not_4 (not_4_out, A3);
  xor xor_4 (xor_4_out, B3, A3);
  Multiplexer multiplexer_1 (.in0(and_1_out), .in1(or_1_out), .out(multiplexer_1_out), .sel(S0));  // open: en
  Multiplexer multiplexer_2 (.in0(not_1_out), .in1(xor_1_out), .out(multiplexer_2_out), .sel(S0));  // open: en
  Multiplexer multiplexer_3 (.in0(and_2_out), .in1(or_2_out), .out(multiplexer_3_out), .sel(S0));  // open: en
  Multiplexer multiplexer_4 (.in0(not_2_out), .in1(xor_2_out), .out(multiplexer_4_out), .sel(S0));  // open: en
  Multiplexer multiplexer_5 (.in0(and_3_out), .in1(or_3_out), .out(multiplexer_5_out), .sel(S0));  // open: en
  Multiplexer multiplexer_6 (.in0(not_3_out), .in1(xor_3_out), .out(multiplexer_6_out), .sel(S0));  // open: en
  Multiplexer multiplexer_7 (.in0(and_4_out), .in1(or_4_out), .out(multiplexer_7_out), .sel(S0));  // open: en
  Multiplexer multiplexer_8 (.in0(not_4_out), .in1(xor_4_out), .out(multiplexer_8_out), .sel(S0));  // open: en
  Multiplexer multiplexer_9 (.in0(multiplexer_1_out), .in1(multiplexer_2_out), .out(F0), .sel(S1));  // open: en
  Multiplexer multiplexer_10 (.in0(multiplexer_3_out), .in1(multiplexer_4_out), .out(F1), .sel(S1));  // open: en
  Multiplexer multiplexer_11 (.in0(multiplexer_5_out), .in1(multiplexer_6_out), .out(F2), .sel(S1));  // open: en
  Multiplexer multiplexer_12 (.in0(multiplexer_7_out), .in1(multiplexer_8_out), .out(F3), .sel(S1));  // open: en
endmodule

module \unidade_aritmética_de_4_bits  (
  input  A3,
  input  A2,
  input  A1,
  input  A0,
  input  B3,
  input  B2,
  input  B1,
  input  B0,
  input  S1,
  input  S0,
  input  Cin,
  output Cout,
  output F3,
  output F2,
  output F1,
  output F0
);

  wire adder_1_cout, adder_2_cout, adder_3_cout, and_1_out, multiplexer_1_out, multiplexer_2_out,
       multiplexer_3_out, multiplexer_4_out, multiplexer_5_out, multiplexer_6_out, multiplexer_7_out,
       multiplexer_8_out, multiplexer_9_out, multiplexer_10_out, multiplexer_11_out, multiplexer_12_out,
       not_1_out, not_2_out, not_3_out, not_4_out, or_1_out, xor_1_out;

  xor xor_1 (xor_1_out, S0, S1);
  not not_1 (not_1_out, B0);
  not not_2 (not_2_out, B1);
  not not_3 (not_3_out, B2);
  not not_4 (not_4_out, B3);
  or or_1 (or_1_out, Cin, ~Cin);  // OR_Gate
  and and_1 (and_1_out, or_1_out, xor_1_out);
  Multiplexer multiplexer_1 (.in0(B0), .in1(not_1_out), .out(multiplexer_1_out), .sel(S0));  // open: en
  Multiplexer multiplexer_2 (
    .in0(multiplexer_1_out), .in1(multiplexer_3_out), .out(multiplexer_2_out), .sel(S1));  // open: en
  Multiplexer multiplexer_3 (.in0(S0), .in1(A0), .out(multiplexer_3_out), .sel(S0));  // open: en
  Multiplexer multiplexer_4 (.in0(B1), .in1(not_2_out), .out(multiplexer_4_out), .sel(S0));  // open: en
  Multiplexer multiplexer_5 (
    .in0(multiplexer_4_out), .in1(multiplexer_6_out), .out(multiplexer_5_out), .sel(S1));  // open: en
  Multiplexer multiplexer_6 (.in0(S0), .in1(A1), .out(multiplexer_6_out), .sel(S0));  // open: en
  Multiplexer multiplexer_7 (.in0(B2), .in1(not_3_out), .out(multiplexer_7_out), .sel(S0));  // open: en
  Multiplexer multiplexer_8 (
    .in0(multiplexer_7_out), .in1(multiplexer_9_out), .out(multiplexer_8_out), .sel(S1));  // open: en
  Multiplexer multiplexer_9 (.in0(S0), .in1(A2), .out(multiplexer_9_out), .sel(S0));  // open: en
  Multiplexer multiplexer_10 (.in0(B3), .in1(not_4_out), .out(multiplexer_10_out), .sel(S0));  // open: en
  Multiplexer multiplexer_11 (
    .in0(multiplexer_10_out), .in1(multiplexer_12_out), .out(multiplexer_11_out), .sel(S1));  // open: en
  Multiplexer multiplexer_12 (.in0(S0), .in1(A3), .out(multiplexer_12_out), .sel(S0));  // open: en
  Adder #(.width(1)) adder_1 (.a(A0), .b(multiplexer_2_out), .out(F0), .cin(and_1_out), .cout(adder_1_cout));
  Adder #(.width(1)) adder_2 (.a(A1), .b(multiplexer_5_out), .out(F1), .cin(adder_1_cout), .cout(adder_2_cout));
  Adder #(.width(1)) adder_3 (.a(A2), .b(multiplexer_8_out), .out(F2), .cin(adder_2_cout), .cout(adder_3_cout));
  Adder #(.width(1)) adder_4 (.a(A3), .b(multiplexer_11_out), .out(F3), .cin(adder_3_cout), .cout(Cout));
endmodule

module mux (
  input  A,
  input  SEL,
  input  B,
  output out_4
);

  wire and_1_out, and_2_out, not_1_out;

  not not_1 (not_1_out, SEL);
  and and_1 (and_1_out, A, not_1_out);
  or or_1 (out_4, and_1_out, and_2_out);
  and and_2 (and_2_out, SEL, B);
endmodule

module demux (
  input  A,
  input  SEL,
  output out_3,
  output out_4
);

  wire not_1_out;

  and and_1 (out_3, A, not_1_out);
  not not_1 (not_1_out, SEL);
  and and_2 (out_4, A, SEL);
endmodule

module MS___Meio_Somador (
  input  in_1,
  input  in_2,
  output out_3
);

  wire and_1_out;

  and and_1 (and_1_out, in_1, in_2);
  xor xor_1 (out_3, in_1, in_2);
endmodule

module SC___Somador_Completo (
  input  in_1,
  input  in_2,
  output out_3,
  output out_4
);

  wire and_1_out, and_2_out, xor_1_out;

  or or_1 (out_3, and_1_out, and_2_out);
  and and_1 (and_1_out, in_2, in_1);
  and and_2 (and_2_out, xor_1_out, in_1);
  xor xor_1 (xor_1_out, in_2, in_1);
  xor xor_2 (out_4, in_1, xor_1_out);
endmodule

module \unidade_lógica_de_8_bits  (
  input  in_1,
  input  in_2,
  input  in_3,
  input  in_4,
  input  A3,
  input  A2,
  input  A1,
  input  A0,
  input  in_9,
  input  in_10,
  input  in_11,
  input  in_12,
  input  B3,
  input  B2,
  input  B1,
  input  B0,
  input  S1,
  input  S0,
  output F3,
  output F2,
  output F1,
  output F0
);

  wire and_1_out, and_2_out, and_3_out, and_4_out, multiplexer_1_out, multiplexer_2_out, multiplexer_3_out,
       multiplexer_4_out, multiplexer_5_out, multiplexer_6_out, multiplexer_7_out, multiplexer_8_out,
       not_1_out, not_2_out, not_3_out, not_4_out, or_1_out, or_2_out, or_3_out, or_4_out, xor_1_out,
       xor_2_out, xor_3_out, xor_4_out;

  and and_1 (and_1_out, B0, A0);
  or or_1 (or_1_out, B0, A0);
  not not_1 (not_1_out, A0);
  xor xor_1 (xor_1_out, B0, A0);
  and and_2 (and_2_out, B1, A1);
  or or_2 (or_2_out, B1, A1);
  not not_2 (not_2_out, A1);
  xor xor_2 (xor_2_out, B1, A1);
  and and_3 (and_3_out, B2, A2);
  or or_3 (or_3_out, B2, A2);
  not not_3 (not_3_out, A2);
  xor xor_3 (xor_3_out, B2, A2);
  and and_4 (and_4_out, B3, A3);
  or or_4 (or_4_out, B3, A3);
  not not_4 (not_4_out, A3);
  xor xor_4 (xor_4_out, B3, A3);
  Multiplexer multiplexer_1 (.in0(and_1_out), .in1(or_1_out), .out(multiplexer_1_out), .sel(S0));  // open: en
  Multiplexer multiplexer_2 (.in0(not_1_out), .in1(xor_1_out), .out(multiplexer_2_out), .sel(S0));  // open: en
  Multiplexer multiplexer_3 (.in0(and_2_out), .in1(or_2_out), .out(multiplexer_3_out), .sel(S0));  // open: en
  Multiplexer multiplexer_4 (.in0(not_2_out), .in1(xor_2_out), .out(multiplexer_4_out), .sel(S0));  // open: en
  Multiplexer multiplexer_5 (.in0(and_3_out), .in1(or_3_out), .out(multiplexer_5_out), .sel(S0));  // open: en
  Multiplexer multiplexer_6 (.in0(not_3_out), .in1(xor_3_out), .out(multiplexer_6_out), .sel(S0));  // open: en
  Multiplexer multiplexer_7 (.in0(and_4_out), .in1(or_4_out), .out(multiplexer_7_out), .sel(S0));  // open: en
  Multiplexer multiplexer_8 (.in0(not_4_out), .in1(xor_4_out), .out(multiplexer_8_out), .sel(S0));  // open: en
  Multiplexer multiplexer_9 (.in0(multiplexer_1_out), .in1(multiplexer_2_out), .out(F0), .sel(S1));  // open: en
  Multiplexer multiplexer_10 (.in0(multiplexer_3_out), .in1(multiplexer_4_out), .out(F1), .sel(S1));  // open: en
  Multiplexer multiplexer_11 (.in0(multiplexer_5_out), .in1(multiplexer_6_out), .out(F2), .sel(S1));  // open: en
  Multiplexer multiplexer_12 (.in0(multiplexer_7_out), .in1(multiplexer_8_out), .out(F3), .sel(S1));  // open: en
endmodule

module ULA_de_8_bits (
  input  A7,
  input  A6,
  input  A5,
  input  A4,
  input  A3,
  input  A2,
  input  A1,
  input  A0,
  input  B7,
  input  B6,
  input  B5,
  input  B4,
  input  B3,
  input  B2,
  input  B1,
  input  B0,
  input  S1,
  input  S0,
  output F3,
  output F2,
  output F1,
  output F0
);
endmodule

module _8_1 (
  input  S2,
  input  S1,
  input  S0,
  input  ENTRADA,
  input  in_5,
  input  in_6,
  input  in_7,
  input  in_8,
  input  in_9,
  input  in_10,
  input  in_11
);

  // AND_Gate _000 has open pins: in0=ENTRADA, in1=in_5, out=open
  // AND_Gate _000_2 is placed but not wired
endmodule

module _1_8 (
  input  S2,
  input  S1,
  input  S0,
  input  A
);

  // AND_Gate _000 is placed but not wired
endmodule

// 101=A-B
module ULA_minimizado (
  input  A7,
  input  A6,
  input  A5,
  input  A4,
  input  A3,
  input  A2,
  input  A1,
  input  A0,
  input  B7,
  input  B6,
  input  B5,
  input  B4,
  input  B3,
  input  B2,
  input  B1,
  input  B0,
  input  S2,
  input  S1,
  input  S0,
  output CY,
  output BW,
  output C7,
  output C6,
  output C5,
  output C4,
  output C3,
  output C2,
  output C1,
  output C0
);

  \ULA_não_minimizado  \ula_não_minimizado_1  (
    .C7(C7), .C6(C6), .C5(C5), .C4(C4), .C3(C3), .C2(C2), .C1(C1), .C0(C0), .A0(A0), .A1(A1), .A2(A2),
    .A3(A3), .A4(A4), .A5(A5), .A6(A6), .A7(A7), .B0(B0), .B1(B1), .B2(B2), .B3(B3), .B4(B4), .B5(B5),
    .B6(B6), .B7(B7), .S2(S2), .S1(S1), .S0(S0), .Carry(CY), .Borrow(BW));

  // Notes on the sheet:
  //   S2, S1, S0:
  //   000 - A+0
  //   001 - B+0
  //   010 - A+1
  //   011 - B+1
  //   100 - A+B
  //   101 - A-B
  //   110 - A AND B
  //   111 - A OR B
endmodule

module \ULA_não_minimizado  (
  input  S0,
  input  S1,
  input  S2,
  input  A0,
  input  A1,
  input  A2,
  input  A3,
  input  A4,
  input  A5,
  input  A6,
  input  A7,
  input  B0,
  input  B1,
  input  B2,
  input  B3,
  input  B4,
  input  B5,
  input  B6,
  input  B7,
  output Carry,
  output Borrow,
  output C7,
  output C6,
  output C5,
  output C4,
  output C3,
  output C2,
  output C1,
  output C0
);

  wire n000_a_0_1_c0, n000_a_0_1_c1, n000_a_0_1_c2, n000_a_0_1_c3, n000_a_0_1_c4, n000_a_0_1_c5,
       n000_a_0_1_c6, n000_a_0_1_c7, n001_b_0_1_c0, n001_b_0_1_c1, n001_b_0_1_c2, n001_b_0_1_c3,
       n001_b_0_1_c4, n001_b_0_1_c5, n001_b_0_1_c6, n001_b_0_1_c7, n010_a_1_1_c0, n010_a_1_1_c1,
       n010_a_1_1_c2, n010_a_1_1_c3, n010_a_1_1_c4, n010_a_1_1_c5, n010_a_1_1_c6, n010_a_1_1_c7,
       n011_b_1_1_c0, n011_b_1_1_c1, n011_b_1_1_c2, n011_b_1_1_c3, n011_b_1_1_c4, n011_b_1_1_c5,
       n011_b_1_1_c6, n011_b_1_1_c7, n100_a_b_1_c0, n100_a_b_1_c1, n100_a_b_1_c2, n100_a_b_1_c3,
       n100_a_b_1_c4, n100_a_b_1_c5, n100_a_b_1_c6, n100_a_b_1_c7, n101_a_b_1_c0, n101_a_b_1_c1,
       n101_a_b_1_c2, n101_a_b_1_c3, n101_a_b_1_c4, n101_a_b_1_c5, n101_a_b_1_c6, n101_a_b_1_c7,
       n110_a_and_b_1_c0, n110_a_and_b_1_c1, n110_a_and_b_1_c2, n110_a_and_b_1_c3, n110_a_and_b_1_c4,
       n110_a_and_b_1_c5, n110_a_and_b_1_c6, n110_a_and_b_1_c7, n111_a_or_b_1_c0, n111_a_or_b_1_c1,
       n111_a_or_b_1_c2, n111_a_or_b_1_c3, n111_a_or_b_1_c4, n111_a_or_b_1_c5, n111_a_or_b_1_c6,
       n111_a_or_b_1_c7;

  _000__A_0 u_000_a_0_1 (
    .A0(A0), .A1(A1), .A2(A2), .A3(A3), .A4(A4), .A5(A5), .A6(A6), .A7(A7), .B0(B0), .B1(B1), .B2(B2),
    .B3(B3), .B4(B4), .B5(B5), .B6(B6), .B7(B7), .C7(n000_a_0_1_c7), .C6(n000_a_0_1_c6), .C5(n000_a_0_1_c5),
    .C4(n000_a_0_1_c4), .C3(n000_a_0_1_c3), .C2(n000_a_0_1_c2), .C1(n000_a_0_1_c1), .C0(n000_a_0_1_c0),
    .S2(S2), .S1(S1), .S0(S0));
  _001__B_0 u_001_b_0_1 (
    .A0(A0), .A1(A1), .A2(A2), .A3(A3), .A4(A4), .A5(A5), .A6(A6), .A7(A7), .B0(B0), .B1(B1), .B2(B2),
    .B3(B3), .B4(B4), .B5(B5), .B6(B6), .B7(B7), .C7(n001_b_0_1_c7), .C6(n001_b_0_1_c6), .C5(n001_b_0_1_c5),
    .C4(n001_b_0_1_c4), .C3(n001_b_0_1_c3), .C2(n001_b_0_1_c2), .C1(n001_b_0_1_c1), .C0(n001_b_0_1_c0),
    .S2(S2), .S1(S1), .S0(S0));
  teste teste_1 (
    .SAIDA_0(n000_a_0_1_c0), .SAIDA_0_2(n001_b_0_1_c0), .SAIDA_0_3(n010_a_1_1_c0), .SAIDA_0_4(n011_b_1_1_c0),
    .SAIDA_0_5(n100_a_b_1_c0), .SAIDA_0_6(n101_a_b_1_c0), .SAIDA_0_7(n110_a_and_b_1_c5),
    .SAIDA_0_8(n111_a_or_b_1_c0), .SAIDA_1(n000_a_0_1_c1), .SAIDA_1_2(n001_b_0_1_c1),
    .SAIDA_1_3(n010_a_1_1_c1), .SAIDA_1_4(n011_b_1_1_c1), .SAIDA_1_5(n100_a_b_1_c1),
    .SAIDA_1_6(n101_a_b_1_c1), .SAIDA_1_7(n110_a_and_b_1_c1), .SAIDA_1_8(n111_a_or_b_1_c1),
    .SAIDA_2(n000_a_0_1_c2), .SAIDA_2_2(n001_b_0_1_c2), .SAIDA_2_3(n010_a_1_1_c2), .SAIDA_2_4(n011_b_1_1_c2),
    .SAIDA_2_5(n100_a_b_1_c2), .SAIDA_2_6(n101_a_b_1_c2), .SAIDA_2_7(n110_a_and_b_1_c0),
    .SAIDA_2_8(n111_a_or_b_1_c2), .SAIDA_3(n000_a_0_1_c3), .SAIDA_3_2(n001_b_0_1_c3),
    .SAIDA_3_3(n010_a_1_1_c3), .SAIDA_3_4(n011_b_1_1_c3), .SAIDA_3_5(n100_a_b_1_c3),
    .SAIDA_3_6(n101_a_b_1_c3), .SAIDA_3_7(n110_a_and_b_1_c2), .SAIDA_3_8(n111_a_or_b_1_c3), .C0(C0),
    .SAIDA_4(n000_a_0_1_c4), .SAIDA_4_2(n001_b_0_1_c4), .SAIDA_4_3(n010_a_1_1_c4), .SAIDA_4_4(n011_b_1_1_c4),
    .SAIDA_4_5(n100_a_b_1_c4), .SAIDA_4_6(n101_a_b_1_c4), .SAIDA_4_7(n110_a_and_b_1_c3),
    .SAIDA_4_8(n111_a_or_b_1_c4), .SAIDA_5(n000_a_0_1_c5), .SAIDA_5_2(n001_b_0_1_c5),
    .SAIDA_5_3(n010_a_1_1_c5), .SAIDA_5_4(n011_b_1_1_c5), .SAIDA_5_5(n100_a_b_1_c5),
    .SAIDA_5_6(n101_a_b_1_c5), .SAIDA_5_7(n110_a_and_b_1_c4), .SAIDA_5_8(n111_a_or_b_1_c5),
    .SAIDA_6(n000_a_0_1_c6), .SAIDA_6_2(n001_b_0_1_c6), .SAIDA_6_3(n010_a_1_1_c6), .SAIDA_6_4(n011_b_1_1_c6),
    .SAIDA_6_5(n100_a_b_1_c6), .SAIDA_6_6(n101_a_b_1_c6), .SAIDA_6_7(n110_a_and_b_1_c6),
    .SAIDA_6_8(n111_a_or_b_1_c6), .SAIDA_7(n000_a_0_1_c7), .SAIDA_7_2(n001_b_0_1_c7),
    .SAIDA_7_3(n010_a_1_1_c7), .SAIDA_7_4(n011_b_1_1_c7), .SAIDA_7_5(n100_a_b_1_c7),
    .SAIDA_7_6(n101_a_b_1_c7), .SAIDA_7_7(n110_a_and_b_1_c7), .SAIDA_7_8(n111_a_or_b_1_c7), .C1(C1), .C2(C2),
    .C3(C3), .C4(C4), .C5(C5), .C6(C6), .C7(C7));
  _010__A_1 u_010_a_1_1 (
    .A0(A0), .A1(A1), .A2(A2), .A3(A3), .A4(A4), .A5(A5), .A6(A6), .A7(A7), .B0(B0), .B1(B1), .B2(B2),
    .B3(B3), .B4(B4), .B5(B5), .B6(B6), .B7(B7), .C7(n010_a_1_1_c7), .C6(n010_a_1_1_c6), .C5(n010_a_1_1_c5),
    .C4(n010_a_1_1_c4), .C3(n010_a_1_1_c3), .C2(n010_a_1_1_c2), .C1(n010_a_1_1_c1), .C0(n010_a_1_1_c0),
    .S2(S2), .S1(S1), .S0(S0));
  _011__B_1 u_011_b_1_1 (
    .A0(A0), .A1(A1), .A2(A2), .A3(A3), .A4(A4), .A5(A5), .A6(A6), .A7(A7), .B0(B0), .B1(B1), .B2(B2),
    .B3(B3), .B4(B4), .B5(B5), .B6(B6), .B7(B7), .C7(n011_b_1_1_c7), .C6(n011_b_1_1_c6), .C5(n011_b_1_1_c5),
    .C4(n011_b_1_1_c4), .C3(n011_b_1_1_c3), .C2(n011_b_1_1_c2), .C1(n011_b_1_1_c1), .C0(n011_b_1_1_c0),
    .S2(S2), .S1(S1), .S0(S0));
  _100__A_B u_100_a_b_1 (
    .A0(A0), .A1(A1), .A2(A2), .A3(A3), .A4(A4), .A5(A5), .A6(A6), .A7(A7), .B0(B0), .B1(B1), .B2(B2),
    .B3(B3), .B4(B4), .B5(B5), .B6(B6), .B7(B7), .C7(n100_a_b_1_c7), .C6(n100_a_b_1_c6), .C5(n100_a_b_1_c5),
    .C4(n100_a_b_1_c4), .C3(n100_a_b_1_c3), .C2(n100_a_b_1_c2), .C1(n100_a_b_1_c1), .C0(n100_a_b_1_c0),
    .S2(S2), .S1(S1), .S0(S0), .Carry(Carry));
  _101__A_B u_101_a_b_1 (
    .A0(A0), .A1(A1), .A2(A2), .A3(A3), .A4(A4), .A5(A5), .A6(A6), .A7(A7), .B0(B0), .B1(B1), .B2(B2),
    .B3(B3), .B4(B4), .B5(B5), .B6(B6), .B7(B7), .C7(n101_a_b_1_c7), .C6(n101_a_b_1_c6), .C5(n101_a_b_1_c5),
    .C4(n101_a_b_1_c4), .C3(n101_a_b_1_c3), .C2(n101_a_b_1_c2), .C1(n101_a_b_1_c1), .C0(n101_a_b_1_c0),
    .S2(S2), .S1(S1), .S0(S0), .Borrow(Borrow));
  _110__A_AND_B u_110_a_and_b_1 (
    .S2(S2), .S1(S1), .S0(S0), .A7(A7), .B7(B7), .A6(A6), .B6(B6), .A5(A5), .B5(B5), .A4(A4), .B4(B4),
    .A3(A3), .B3(B3), .A2(A2), .B2(B2), .A1(A1), .B1(B1), .A0(A0), .B0(B0), .C7(n110_a_and_b_1_c7),
    .C6(n110_a_and_b_1_c6), .C4(n110_a_and_b_1_c4), .C3(n110_a_and_b_1_c3), .C2(n110_a_and_b_1_c2),
    .C1(n110_a_and_b_1_c1), .C0(n110_a_and_b_1_c0), .C5(n110_a_and_b_1_c5));
  _111__A_OR_B u_111_a_or_b_1 (
    .A0(A0), .A1(A1), .A2(A2), .A3(A3), .A4(A4), .A5(A5), .A6(A6), .A7(A7), .B0(B1), .B1(B2), .B2(B3),
    .B3(B4), .B4(B4), .B5(B5), .B6(B6), .B7(B7), .C7(n111_a_or_b_1_c7), .C6(n111_a_or_b_1_c6),
    .C5(n111_a_or_b_1_c5), .C4(n111_a_or_b_1_c4), .C3(n111_a_or_b_1_c3), .C2(n111_a_or_b_1_c2),
    .C1(n111_a_or_b_1_c1), .C0(n111_a_or_b_1_c0), .S2(S2), .S1(S1), .S0(S0));
endmodule

module Rascunho (
  input  A7,
  input  A6,
  input  A5,
  input  A4,
  input  A3,
  input  A2,
  input  A1,
  input  A0,
  input  B7,
  input  B6,
  input  B5,
  input  B4,
  input  B3,
  input  B2,
  input  B1,
  input  B0,
  input  S2,
  input  S1,
  input  S0,
  input  SAIDA_0,
  input  SAIDA_4,
  input  SAIDA_0_2,
  input  SAIDA_4_2,
  input  SAIDA_0_3,
  input  SAIDA_4_3,
  input  SAIDA_0_4,
  input  SAIDA_4_4,
  input  SAIDA_0_5,
  input  SAIDA_4_5,
  input  SAIDA_0_6,
  input  SAIDA_4_6,
  input  SAIDA_0_7,
  input  SAIDA_4_7,
  input  SAIDA_0_8,
  input  SAIDA_4_8,
  input  SAIDA_1,
  input  SAIDA_5,
  input  SAIDA_1_2,
  input  SAIDA_5_2,
  input  SAIDA_1_3,
  input  SAIDA_5_3,
  input  SAIDA_1_4,
  input  SAIDA_5_4,
  input  SAIDA_1_5,
  input  SAIDA_5_5,
  input  SAIDA_1_6,
  input  SAIDA_5_6,
  input  A,
  input  B,
  input  SAIDA_1_7,
  input  SAIDA_5_7,
  input  SAIDA_1_8,
  input  SAIDA_5_8,
  input  SAIDA_2,
  input  SAIDA_6,
  input  SAIDA_2_2,
  input  SAIDA_6_2,
  input  A_2,
  input  SAIDA_2_3,
  input  SAIDA_6_3,
  input  B_2,
  input  SAIDA_2_4,
  input  SAIDA_6_4,
  input  SAIDA_2_5,
  input  SAIDA_6_5,
  input  SAIDA_2_6,
  input  SAIDA_6_6,
  input  SAIDA_2_7,
  input  SAIDA_6_7,
  input  SAIDA_2_8,
  input  SAIDA_6_8,
  input  SAIDA_3,
  input  SAIDA_7,
  input  SAIDA_3_2,
  input  SAIDA_7_2,
  input  SAIDA_3_3,
  input  SAIDA_7_3,
  input  SAIDA_3_4,
  input  SAIDA_7_4,
  input  SAIDA_3_5,
  input  SAIDA_7_5,
  input  SAIDA_3_6,
  input  SAIDA_7_6,
  input  SAIDA_3_7,
  input  SAIDA_7_7,
  input  SAIDA_3_8,
  input  SAIDA_7_8,
  output C0,
  output C4,
  output Carry_ou_Borrow,
  output C7,
  output C6,
  output C1,
  output C5,
  output C5_2,
  output C4_2,
  output C3,
  output C2,
  output C1_2,
  output C0_2,
  output S0_2,
  output C2_2,
  output C6_2,
  output S,
  output C3_2,
  output C7_2
);

  wire and_1_out, not_1_out, not_2_out, not_3_out, not_4_out, xor_1_out;

  and and_1 (and_1_out, B, not_1_out);
  or or_1 (S, A, and_1_out);
  not not_1 (not_1_out, B);
  xor xor_1 (xor_1_out, A_2, B_2);
  buf xor_2 (S0_2, xor_1_out);  // XOR_Gate
  not not_2 (not_2_out, S0);
  not not_3 (not_3_out, S2);
  not not_4 (not_4_out, S1);
  // AND_Gate and_2 has open pins: in0=not_3_out, in1=not_4_out, in2=not_2_out, out=open
  or or_2 (C0, SAIDA_0, SAIDA_0_2, SAIDA_0_3, SAIDA_0_4, SAIDA_0_5, SAIDA_0_6, SAIDA_0_7, SAIDA_0_8);
  or or_3 (C1, SAIDA_1, SAIDA_1_2, SAIDA_1_3, SAIDA_1_4, SAIDA_1_5, SAIDA_1_6, SAIDA_1_7, SAIDA_1_8);
  or or_4 (C2_2, SAIDA_2, SAIDA_2_2, SAIDA_2_3, SAIDA_2_4, SAIDA_2_5, SAIDA_2_6, SAIDA_2_7, SAIDA_2_8);
  or or_5 (C3_2, SAIDA_3, SAIDA_3_2, SAIDA_3_3, SAIDA_3_4, SAIDA_3_5, SAIDA_3_6, SAIDA_3_7, SAIDA_3_8);
  or or_6 (C4, SAIDA_4, SAIDA_4_2, SAIDA_4_3, SAIDA_4_4, SAIDA_4_5, SAIDA_4_6, SAIDA_4_7, SAIDA_4_8);
  or or_7 (C5, SAIDA_5, SAIDA_5_2, SAIDA_5_3, SAIDA_5_4, SAIDA_5_5, SAIDA_5_6, SAIDA_5_7, SAIDA_5_8);
  or or_8 (C6_2, SAIDA_6, SAIDA_6_2, SAIDA_6_3, SAIDA_6_4, SAIDA_6_5, SAIDA_6_6, SAIDA_6_7, SAIDA_6_8);
  or or_9 (C7_2, SAIDA_7, SAIDA_7_2, SAIDA_7_3, SAIDA_7_4, SAIDA_7_5, SAIDA_7_6, SAIDA_7_7, SAIDA_7_8);

  // Notes on the sheet:
  //   000-A+0=A
endmodule

module _000__A_0 (
  input  A7,
  input  B7,
  input  A6,
  input  B6,
  input  A5,
  input  B5,
  input  A4,
  input  B4,
  input  A3,
  input  B3,
  input  A2,
  input  B2,
  input  A1,
  input  B1,
  input  A0,
  input  B0,
  input  S0,
  input  S1,
  input  S2,
  output C7,
  output C6,
  output C5,
  output C4,
  output C3,
  output C2,
  output C1,
  output C0
);

  wire and_2_out, and_3_out, and_5_out, and_7_out, and_9_out, and_11_out, and_13_out, and_15_out, and_16_out,
       not_1_out, not_2_out, not_3_out, not_4_out, not_5_out, not_6_out, not_7_out, not_8_out, not_9_out,
       not_10_out, not_11_out, or_1_out, or_2_out, or_3_out, or_4_out, or_5_out, or_6_out, or_7_out, or_8_out;

  and and_1 (C7, or_1_out, and_2_out);
  not not_1 (not_1_out, S0);
  not not_2 (not_2_out, S1);
  and and_2 (and_2_out, not_1_out, not_2_out, not_3_out);
  not not_3 (not_3_out, S2);
  not not_4 (not_4_out, B7);
  and and_3 (and_3_out, B7, not_4_out);
  or or_1 (or_1_out, A7, and_3_out);
  and and_4 (C6, or_2_out, and_2_out);
  not not_5 (not_5_out, B6);
  and and_5 (and_5_out, B6, not_5_out);
  or or_2 (or_2_out, A6, and_5_out);
  and and_6 (C5, or_3_out, and_2_out);
  not not_6 (not_6_out, B5);
  and and_7 (and_7_out, B5, not_6_out);
  or or_3 (or_3_out, A5, and_7_out);
  and and_8 (C4, or_4_out, and_2_out);
  not not_7 (not_7_out, B4);
  and and_9 (and_9_out, B4, not_7_out);
  or or_4 (or_4_out, A4, and_9_out);
  and and_10 (C3, or_5_out, and_2_out);
  not not_8 (not_8_out, B3);
  and and_11 (and_11_out, B3, not_8_out);
  or or_5 (or_5_out, A3, and_11_out);
  and and_12 (C2, or_6_out, and_2_out);
  not not_9 (not_9_out, B2);
  and and_13 (and_13_out, B2, not_9_out);
  or or_6 (or_6_out, A2, and_13_out);
  and and_14 (C1, or_7_out, and_2_out);
  not not_10 (not_10_out, B1);
  and and_15 (and_15_out, B1, not_10_out);
  or or_7 (or_7_out, A1, and_15_out);
  not not_11 (not_11_out, B0);
  and and_16 (and_16_out, B0, not_11_out);
  or or_8 (or_8_out, A0, and_16_out);
  and and_17 (C0, or_8_out, and_2_out);
endmodule

module _001__B_0 (
  input  B7,
  input  A7,
  input  B6,
  input  A6,
  input  B5,
  input  A5,
  input  B4,
  input  A4,
  input  B3,
  input  A3,
  input  B2,
  input  A2,
  input  B1,
  input  A1,
  input  B0,
  input  A0,
  input  S0,
  input  S1,
  input  S2,
  output C7,
  output C6,
  output C5,
  output C4,
  output C3,
  output C2,
  output C1,
  output C0
);

  wire and_2_out, and_4_out, and_5_out, and_7_out, and_9_out, and_11_out, and_13_out, and_14_out, and_16_out,
       not_1_out, not_2_out, not_3_out, not_4_out, not_5_out, not_6_out, not_7_out, not_8_out, not_9_out,
       not_10_out, or_1_out, or_2_out, or_3_out, or_4_out, or_5_out, or_6_out, or_7_out, or_8_out;

  and and_1 (C7, or_1_out, and_4_out);
  not not_1 (not_1_out, S1);
  not not_2 (not_2_out, S2);
  not not_3 (not_3_out, A7);
  and and_2 (and_2_out, A7, not_3_out);
  or or_1 (or_1_out, B7, and_2_out);
  and and_3 (C6, or_2_out, and_4_out);
  and and_4 (and_4_out, S0, not_1_out, not_2_out);
  not not_4 (not_4_out, A6);
  and and_5 (and_5_out, A6, not_4_out);
  or or_2 (or_2_out, B6, and_5_out);
  and and_6 (C5, or_3_out, and_4_out);
  not not_5 (not_5_out, A5);
  and and_7 (and_7_out, A5, not_5_out);
  or or_3 (or_3_out, B5, and_7_out);
  and and_8 (C4, or_4_out, and_4_out);
  not not_6 (not_6_out, A4);
  and and_9 (and_9_out, A4, not_6_out);
  or or_4 (or_4_out, B4, and_9_out);
  and and_10 (C3, or_5_out, and_4_out);
  not not_7 (not_7_out, A3);
  and and_11 (and_11_out, A3, not_7_out);
  or or_5 (or_5_out, B3, and_11_out);
  and and_12 (C2, or_6_out, and_4_out);
  not not_8 (not_8_out, A2);
  and and_13 (and_13_out, A2, not_8_out);
  or or_6 (or_6_out, B2, and_13_out);
  not not_9 (not_9_out, A1);
  and and_14 (and_14_out, A1, not_9_out);
  or or_7 (or_7_out, B1, and_14_out);
  and and_15 (C1, or_7_out, and_4_out);
  not not_10 (not_10_out, A0);
  and and_16 (and_16_out, A0, not_10_out);
  or or_8 (or_8_out, B0, and_16_out);
  and and_17 (C0, or_8_out, and_4_out);
endmodule

module _010__A_1 (
  input  A7,
  input  B7,
  input  A6,
  input  B6,
  input  A5,
  input  B5,
  input  A4,
  input  B4,
  input  A3,
  input  B3,
  input  A2,
  input  B2,
  input  A1,
  input  B1,
  input  A0,
  input  B0,
  input  S0,
  input  S1,
  input  S2,
  output C7,
  output C6,
  output C5,
  output C4,
  output C3,
  output C2,
  output C1,
  output C0
);

  wire and_2_out, not_1_out, not_2_out, not_3_out, not_4_out, not_5_out, not_6_out, not_7_out, not_8_out,
       not_9_out, not_10_out, or_1_out, or_2_out, or_3_out, or_4_out, or_5_out, or_6_out, or_7_out, or_8_out,
       or_9_out, or_10_out, or_11_out, or_12_out, or_13_out, or_14_out, or_15_out, or_16_out;

  and and_1 (C7, or_2_out, and_2_out);
  not not_1 (not_1_out, S0);
  and and_2 (and_2_out, not_1_out, S1, not_2_out);
  not not_2 (not_2_out, S2);
  not not_3 (not_3_out, B7);
  or or_1 (or_1_out, B7, not_3_out);
  or or_2 (or_2_out, A7, or_1_out);
  and and_3 (C6, or_4_out, and_2_out);
  not not_4 (not_4_out, B6);
  or or_3 (or_3_out, B6, not_4_out);
  or or_4 (or_4_out, A6, or_3_out);
  and and_4 (C5, or_6_out, and_2_out);
  not not_5 (not_5_out, B5);
  or or_5 (or_5_out, B5, not_5_out);
  or or_6 (or_6_out, A5, or_5_out);
  and and_5 (C4, or_8_out, and_2_out);
  not not_6 (not_6_out, B4);
  or or_7 (or_7_out, B4, not_6_out);
  or or_8 (or_8_out, A4, or_7_out);
  and and_6 (C3, or_10_out, and_2_out);
  not not_7 (not_7_out, B3);
  or or_9 (or_9_out, B3, not_7_out);
  or or_10 (or_10_out, A3, or_9_out);
  and and_7 (C2, or_12_out, and_2_out);
  not not_8 (not_8_out, B2);
  or or_11 (or_11_out, B2, not_8_out);
  or or_12 (or_12_out, A2, or_11_out);
  and and_8 (C1, or_14_out, and_2_out);
  not not_9 (not_9_out, B1);
  or or_13 (or_13_out, B1, not_9_out);
  or or_14 (or_14_out, A1, or_13_out);
  not not_10 (not_10_out, B0);
  or or_15 (or_15_out, B0, not_10_out);
  or or_16 (or_16_out, A0, or_15_out);
  and and_9 (C0, or_16_out, and_2_out);
endmodule

module _011__B_1 (
  input  B7,
  input  A7,
  input  B6,
  input  A6,
  input  B5,
  input  A5,
  input  B4,
  input  A4,
  input  B3,
  input  A3,
  input  B2,
  input  A2,
  input  B1,
  input  A1,
  input  B0,
  input  A0,
  input  S0,
  input  S1,
  input  S2,
  output C7,
  output C6,
  output C5,
  output C4,
  output C3,
  output C2,
  output C1,
  output C0
);

  wire and_2_out, not_1_out, not_2_out, not_3_out, not_4_out, not_5_out, not_6_out, not_7_out, not_8_out,
       not_9_out, or_1_out, or_2_out, or_3_out, or_4_out, or_5_out, or_6_out, or_7_out, or_8_out, or_9_out,
       or_10_out, or_11_out, or_12_out, or_13_out, or_14_out, or_15_out, or_16_out;

  and and_1 (C7, or_2_out, and_2_out);
  and and_2 (and_2_out, S0, S1, not_1_out);
  not not_1 (not_1_out, S2);
  not not_2 (not_2_out, A7);
  or or_1 (or_1_out, A7, not_2_out);
  or or_2 (or_2_out, B7, or_1_out);
  and and_3 (C6, or_4_out, and_2_out);
  not not_3 (not_3_out, A6);
  or or_3 (or_3_out, A6, not_3_out);
  or or_4 (or_4_out, B6, or_3_out);
  and and_4 (C5, or_6_out, and_2_out);
  not not_4 (not_4_out, A5);
  or or_5 (or_5_out, A5, not_4_out);
  or or_6 (or_6_out, B5, or_5_out);
  and and_5 (C4, or_8_out, and_2_out);
  not not_5 (not_5_out, A4);
  or or_7 (or_7_out, A4, not_5_out);
  or or_8 (or_8_out, B4, or_7_out);
  and and_6 (C3, or_10_out, and_2_out);
  not not_6 (not_6_out, A3);
  or or_9 (or_9_out, A3, not_6_out);
  or or_10 (or_10_out, B3, or_9_out);
  and and_7 (C2, or_12_out, and_2_out);
  not not_7 (not_7_out, A2);
  or or_11 (or_11_out, A2, not_7_out);
  or or_12 (or_12_out, B2, or_11_out);
  and and_8 (C1, or_14_out, and_2_out);
  not not_8 (not_8_out, A1);
  or or_13 (or_13_out, A1, not_8_out);
  or or_14 (or_14_out, B1, or_13_out);
  and and_9 (C0, or_16_out, and_2_out);
  not not_9 (not_9_out, A0);
  or or_15 (or_15_out, A0, not_9_out);
  or or_16 (or_16_out, B0, or_15_out);
endmodule

module _100__A_B (
  input  A7,
  input  B7,
  input  A6,
  input  B6,
  input  A5,
  input  B5,
  input  A4,
  input  B4,
  input  A3,
  input  B3,
  input  A2,
  input  B2,
  input  A1,
  input  B1,
  input  A0,
  input  B0,
  input  S0,
  input  S1,
  input  S2,
  output Carry,
  output C7,
  output C6,
  output C5,
  output C4,
  output C3,
  output C2,
  output C1,
  output C0
);

  wire and_1_out, and_2_out, and_4_out, and_5_out, and_6_out, and_8_out, and_9_out, and_11_out, and_13_out,
       and_14_out, and_15_out, and_17_out, and_18_out, and_20_out, and_21_out, and_23_out, not_1_out,
       not_2_out, or_2_out, or_3_out, or_4_out, or_5_out, or_6_out, or_7_out, xor_1_out, xor_2_out,
       xor_3_out, xor_4_out, xor_5_out, xor_6_out, xor_7_out, xor_8_out, xor_9_out, xor_10_out, xor_11_out,
       xor_12_out, xor_13_out, xor_14_out, xor_15_out;

  and and_1 (and_1_out, B7, or_2_out);
  or or_1 (Carry, and_1_out, and_2_out);
  and and_2 (and_2_out, xor_1_out, A7);
  and and_3 (C7, xor_2_out, and_4_out);
  not not_1 (not_1_out, S0);
  not not_2 (not_2_out, S1);
  xor xor_1 (xor_1_out, B7, or_2_out);
  xor xor_2 (xor_2_out, A7, xor_1_out);
  and and_4 (and_4_out, not_1_out, not_2_out, S2);
  and and_5 (and_5_out, B6, or_3_out);
  or or_2 (or_2_out, and_5_out, and_6_out);
  and and_6 (and_6_out, xor_3_out, A6);
  and and_7 (C6, xor_4_out, and_4_out);
  xor xor_3 (xor_3_out, B6, or_3_out);
  xor xor_4 (xor_4_out, A6, xor_3_out);
  and and_8 (and_8_out, B5, or_4_out);
  or or_3 (or_3_out, and_8_out, and_9_out);
  and and_9 (and_9_out, xor_5_out, A5);
  and and_10 (C5, xor_6_out, and_4_out);
  xor xor_5 (xor_5_out, B5, or_4_out);
  xor xor_6 (xor_6_out, A5, xor_5_out);
  and and_11 (and_11_out, B4, or_5_out);
  or or_4 (or_4_out, and_11_out, and_13_out);
  and and_12 (C4, xor_7_out, and_4_out);
  and and_13 (and_13_out, xor_8_out, A4);
  xor xor_7 (xor_7_out, A4, xor_8_out);
  and and_14 (and_14_out, B3, or_6_out);
  xor xor_8 (xor_8_out, B4, or_5_out);
  or or_5 (or_5_out, and_14_out, and_15_out);
  and and_15 (and_15_out, xor_9_out, A3);
  and and_16 (C3, xor_10_out, and_4_out);
  xor xor_9 (xor_9_out, B3, or_6_out);
  xor xor_10 (xor_10_out, A3, xor_9_out);
  and and_17 (and_17_out, B2, or_7_out);
  or or_6 (or_6_out, and_17_out, and_18_out);
  and and_18 (and_18_out, xor_11_out, A2);
  and and_19 (C2, xor_12_out, and_4_out);
  xor xor_11 (xor_11_out, B2, or_7_out);
  xor xor_12 (xor_12_out, A2, xor_11_out);
  and and_20 (and_20_out, B1, and_23_out);
  or or_7 (or_7_out, and_20_out, and_21_out);
  and and_21 (and_21_out, xor_13_out, A1);
  and and_22 (C1, xor_14_out, and_4_out);
  xor xor_13 (xor_13_out, B1, and_23_out);
  xor xor_14 (xor_14_out, A1, xor_13_out);
  and and_23 (and_23_out, A0, B0);
  and and_24 (C0, xor_15_out, and_4_out);
  xor xor_15 (xor_15_out, A0, B0);
endmodule

module _101__A_B (
  input  A0,
  input  B0,
  input  A7,
  input  B7,
  input  A6,
  input  B6,
  input  A5,
  input  B5,
  input  A4,
  input  B4,
  input  A3,
  input  B3,
  input  A2,
  input  B2,
  input  A1,
  input  B1,
  input  S0,
  input  S1,
  input  S2,
  output Borrow,
  output C7,
  output C6,
  output C5,
  output C4,
  output C3,
  output C2,
  output C1,
  output C0
);

  wire and_1_out, and_2_out, and_3_out, and_5_out, and_7_out, and_8_out, and_9_out, and_11_out, and_12_out,
       and_13_out, and_15_out, and_16_out, and_17_out, and_19_out, and_20_out, and_21_out, and_22_out,
       and_23_out, and_24_out, and_26_out, and_27_out, and_28_out, and_31_out, not_1_out, or_2_out, or_3_out,
       or_4_out, or_5_out, or_6_out, or_7_out, xor_1_out, xor_2_out, xor_3_out, xor_4_out, xor_5_out,
       xor_6_out, xor_7_out, xor_8_out, xor_9_out, xor_10_out, xor_11_out, xor_12_out, xor_13_out,
       xor_14_out, xor_15_out;

  and and_1 (and_1_out, B7, or_2_out);
  and and_2 (and_2_out, ~A7, or_2_out);  // AND_Gate
  or or_1 (Borrow, and_1_out, and_2_out, and_3_out);
  and and_3 (and_3_out, ~A7, B7);  // AND_Gate
  and and_4 (C7, and_5_out, xor_1_out);
  xor xor_1 (xor_1_out, xor_2_out, or_2_out);
  and and_5 (and_5_out, S0, not_1_out, S2);
  not not_1 (not_1_out, S1);
  xor xor_2 (xor_2_out, A7, B7);
  or or_2 (or_2_out, and_7_out, and_8_out, and_9_out);
  and and_6 (C6, and_5_out, xor_3_out);
  xor xor_3 (xor_3_out, xor_4_out, or_3_out);
  and and_7 (and_7_out, B6, or_3_out);
  and and_8 (and_8_out, ~A6, or_3_out);  // AND_Gate
  and and_9 (and_9_out, ~A6, B6);  // AND_Gate
  xor xor_4 (xor_4_out, A6, B6);
  or or_3 (or_3_out, and_11_out, and_12_out, and_13_out);
  and and_10 (C5, and_5_out, xor_5_out);
  xor xor_5 (xor_5_out, xor_6_out, or_4_out);
  and and_11 (and_11_out, B5, or_4_out);
  and and_12 (and_12_out, ~A5, or_4_out);  // AND_Gate
  and and_13 (and_13_out, ~A5, B5);  // AND_Gate
  xor xor_6 (xor_6_out, A5, B5);
  or or_4 (or_4_out, and_15_out, and_16_out, and_17_out);
  and and_14 (C4, and_5_out, xor_8_out);
  and and_15 (and_15_out, B4, or_5_out);
  and and_16 (and_16_out, ~A4, or_5_out);  // AND_Gate
  and and_17 (and_17_out, ~A4, B4);  // AND_Gate
  xor xor_7 (xor_7_out, A4, B4);
  xor xor_8 (xor_8_out, xor_7_out, or_5_out);
  or or_5 (or_5_out, and_19_out, and_20_out, and_21_out);
  and and_18 (C3, and_5_out, xor_10_out);
  and and_19 (and_19_out, B3, or_6_out);
  and and_20 (and_20_out, ~A3, or_6_out);  // AND_Gate
  and and_21 (and_21_out, ~A3, B3);  // AND_Gate
  xor xor_9 (xor_9_out, A3, B3);
  xor xor_10 (xor_10_out, xor_9_out, or_6_out);
  or or_6 (or_6_out, and_22_out, and_23_out, and_24_out);
  and and_22 (and_22_out, B2, or_7_out);
  and and_23 (and_23_out, ~A2, or_7_out);  // AND_Gate
  and and_24 (and_24_out, ~A2, B2);  // AND_Gate
  and and_25 (C2, and_5_out, xor_12_out);
  xor xor_11 (xor_11_out, A2, B2);
  xor xor_12 (xor_12_out, xor_11_out, or_7_out);
  or or_7 (or_7_out, and_26_out, and_27_out, and_28_out);
  and and_26 (and_26_out, B1, and_31_out);
  and and_27 (and_27_out, ~A1, and_31_out);  // AND_Gate
  and and_28 (and_28_out, ~A1, B1);  // AND_Gate
  xor xor_13 (xor_13_out, A1, B1);
  and and_29 (C1, and_5_out, xor_14_out);
  xor xor_14 (xor_14_out, xor_13_out, and_31_out);
  and and_30 (C0, xor_15_out, and_5_out);
  and and_31 (and_31_out, ~A0, B0);  // AND_Gate
  xor xor_15 (xor_15_out, A0, B0);
endmodule

module _110__A_AND_B (
  input  S0,
  input  S1,
  input  S2,
  input  A7,
  input  B7,
  input  A6,
  input  B6,
  input  A5,
  input  B5,
  input  A4,
  input  B4,
  input  A3,
  input  B3,
  input  A2,
  input  B2,
  input  A1,
  input  B1,
  input  A0,
  input  B0,
  output C7,
  output C6,
  output C5,
  output C4,
  output C3,
  output C2,
  output C1,
  output C0
);

  wire and_1_out, and_2_out, and_4_out, and_6_out, and_8_out, and_10_out, and_12_out, and_14_out, and_16_out,
       not_1_out;

  not not_1 (not_1_out, S0);
  and and_1 (and_1_out, not_1_out, S1, S2);
  and and_2 (and_2_out, A7, B7);
  and and_3 (C7, and_2_out, and_1_out);
  and and_4 (and_4_out, A6, B6);
  and and_5 (C6, and_4_out, and_1_out);
  and and_6 (and_6_out, A5, B5);
  and and_7 (C5, and_6_out, and_1_out);
  and and_8 (and_8_out, A4, B4);
  and and_9 (C4, and_8_out, and_1_out);
  and and_10 (and_10_out, A3, B3);
  and and_11 (C3, and_10_out, and_1_out);
  and and_12 (and_12_out, A2, B2);
  and and_13 (C2, and_12_out, and_1_out);
  and and_14 (and_14_out, A1, B1);
  and and_15 (C1, and_14_out, and_1_out);
  and and_16 (and_16_out, A0, B0);
  and and_17 (C0, and_16_out, and_1_out);
endmodule

module _111__A_OR_B (
  input  A7,
  input  B7,
  input  A6,
  input  B6,
  input  A5,
  input  B5,
  input  A4,
  input  B4,
  input  A3,
  input  B3,
  input  A2,
  input  B2,
  input  A1,
  input  B1,
  input  A0,
  input  B0,
  input  S0,
  input  S1,
  input  S2,
  output C7,
  output C6,
  output C5,
  output C4,
  output C3,
  output C2,
  output C1,
  output C0
);

  wire and_1_out, or_1_out, or_2_out, or_3_out, or_4_out, or_5_out, or_6_out, or_7_out, or_8_out;

  or or_1 (or_1_out, A7, B7);
  and and_1 (and_1_out, S0, S1, S2);
  and and_2 (C7, or_1_out, and_1_out);
  or or_2 (or_2_out, A6, B6);
  and and_3 (C6, or_2_out, and_1_out);
  or or_3 (or_3_out, A5, B5);
  and and_4 (C5, or_3_out, and_1_out);
  or or_4 (or_4_out, A4, B4);
  and and_5 (C4, or_4_out, and_1_out);
  or or_5 (or_5_out, A3, B3);
  and and_6 (C3, or_5_out, and_1_out);
  or or_6 (or_6_out, A2, B2);
  and and_7 (C2, or_6_out, and_1_out);
  or or_7 (or_7_out, A1, B1);
  and and_8 (C1, or_7_out, and_1_out);
  or or_8 (or_8_out, A0, B0);
  and and_9 (C0, or_8_out, and_1_out);
endmodule

module somador_8_bits (
  input  A7,
  input  B7,
  input  A6,
  input  B6,
  input  A5,
  input  B5,
  input  A4,
  input  B4,
  input  A3,
  input  B3,
  input  A2,
  input  B2,
  input  A1,
  input  B1,
  input  A0,
  input  B0,
  input  S0,
  input  S1,
  input  S2,
  output Carry,
  output S7,
  output S6,
  output S5,
  output S4,
  output S3,
  output S2_2,
  output S1_2,
  output S0_2
);

  wire and_1_out, and_3_out, and_4_out, and_5_out, and_6_out, and_8_out, and_9_out, and_11_out, and_13_out,
       and_14_out, and_16_out, and_17_out, and_18_out, and_20_out, and_21_out, and_23_out, not_1_out,
       not_2_out, or_2_out, or_3_out, or_4_out, or_5_out, or_6_out, or_7_out, xor_1_out, xor_2_out,
       xor_3_out, xor_4_out, xor_5_out, xor_6_out, xor_7_out, xor_8_out, xor_9_out, xor_10_out, xor_11_out,
       xor_12_out, xor_13_out, xor_14_out, xor_15_out;

  and and_1 (and_1_out, B7, or_2_out);
  or or_1 (Carry, and_1_out, and_3_out);
  and and_2 (S7, xor_2_out, and_4_out);
  and and_3 (and_3_out, xor_1_out, A7);
  and and_4 (and_4_out, not_1_out, not_2_out, S2);
  not not_1 (not_1_out, S0);
  not not_2 (not_2_out, S1);
  xor xor_1 (xor_1_out, B7, or_2_out);
  or or_2 (or_2_out, and_5_out, and_6_out);
  xor xor_2 (xor_2_out, A7, xor_1_out);
  and and_5 (and_5_out, B6, or_3_out);
  and and_6 (and_6_out, xor_3_out, A6);
  and and_7 (S6, xor_4_out, and_4_out);
  xor xor_3 (xor_3_out, B6, or_3_out);
  xor xor_4 (xor_4_out, A6, xor_3_out);
  and and_8 (and_8_out, B5, or_4_out);
  or or_3 (or_3_out, and_8_out, and_9_out);
  and and_9 (and_9_out, xor_5_out, A5);
  and and_10 (S5, xor_6_out, and_4_out);
  xor xor_5 (xor_5_out, B5, or_4_out);
  xor xor_6 (xor_6_out, A5, xor_5_out);
  and and_11 (and_11_out, B4, or_5_out);
  or or_4 (or_4_out, and_11_out, and_13_out);
  and and_12 (S4, xor_8_out, and_4_out);
  xor xor_7 (xor_7_out, B4, or_5_out);
  and and_13 (and_13_out, xor_7_out, A4);
  xor xor_8 (xor_8_out, A4, xor_7_out);
  and and_14 (and_14_out, B3, or_6_out);
  or or_5 (or_5_out, and_14_out, and_16_out);
  and and_15 (S3, xor_10_out, and_4_out);
  and and_16 (and_16_out, xor_9_out, A3);
  xor xor_9 (xor_9_out, B3, or_6_out);
  or or_6 (or_6_out, and_17_out, and_18_out);
  xor xor_10 (xor_10_out, A3, xor_9_out);
  and and_17 (and_17_out, B2, or_7_out);
  and and_18 (and_18_out, xor_11_out, A2);
  and and_19 (S2_2, xor_12_out, and_4_out);
  xor xor_11 (xor_11_out, B2, or_7_out);
  xor xor_12 (xor_12_out, A2, xor_11_out);
  and and_20 (and_20_out, B1, and_23_out);
  or or_7 (or_7_out, and_20_out, and_21_out);
  and and_21 (and_21_out, xor_13_out, A1);
  and and_22 (S1_2, xor_14_out, and_4_out);
  xor xor_13 (xor_13_out, B1, and_23_out);
  xor xor_14 (xor_14_out, A1, xor_13_out);
  and and_23 (and_23_out, A0, B0);
  and and_24 (S0_2, xor_15_out, and_4_out);
  xor xor_15 (xor_15_out, A0, B0);
endmodule

module teste (
  input  SAIDA_0,
  input  SAIDA_4,
  input  SAIDA_0_2,
  input  SAIDA_4_2,
  input  SAIDA_0_3,
  input  SAIDA_4_3,
  input  SAIDA_0_4,
  input  SAIDA_4_4,
  input  SAIDA_0_5,
  input  SAIDA_4_5,
  input  SAIDA_0_6,
  input  SAIDA_4_6,
  input  SAIDA_0_7,
  input  SAIDA_4_7,
  input  SAIDA_0_8,
  input  SAIDA_4_8,
  input  SAIDA_1,
  input  SAIDA_5,
  input  SAIDA_1_2,
  input  SAIDA_5_2,
  input  SAIDA_1_3,
  input  SAIDA_5_3,
  input  SAIDA_1_4,
  input  SAIDA_5_4,
  input  SAIDA_1_5,
  input  SAIDA_5_5,
  input  SAIDA_1_6,
  input  SAIDA_5_6,
  input  SAIDA_1_7,
  input  SAIDA_5_7,
  input  SAIDA_1_8,
  input  SAIDA_5_8,
  input  SAIDA_2,
  input  SAIDA_6,
  input  SAIDA_2_2,
  input  SAIDA_6_2,
  input  SAIDA_2_3,
  input  SAIDA_6_3,
  input  SAIDA_2_4,
  input  SAIDA_6_4,
  input  SAIDA_2_5,
  input  SAIDA_6_5,
  input  SAIDA_2_6,
  input  SAIDA_6_6,
  input  SAIDA_2_7,
  input  SAIDA_6_7,
  input  SAIDA_2_8,
  input  SAIDA_6_8,
  input  SAIDA_3,
  input  SAIDA_7,
  input  SAIDA_3_2,
  input  SAIDA_7_2,
  input  SAIDA_3_3,
  input  SAIDA_7_3,
  input  SAIDA_3_4,
  input  SAIDA_7_4,
  input  SAIDA_3_5,
  input  SAIDA_7_5,
  input  SAIDA_3_6,
  input  SAIDA_7_6,
  input  SAIDA_3_7,
  input  SAIDA_7_7,
  input  SAIDA_3_8,
  input  SAIDA_7_8,
  output C0,
  output C4,
  output C1,
  output C5,
  output C2,
  output C6,
  output C3,
  output C7
);

  or or_1 (C0, SAIDA_0, SAIDA_0_2, SAIDA_0_3, SAIDA_0_4, SAIDA_0_5, SAIDA_0_6, SAIDA_0_7, SAIDA_0_8);
  or or_2 (C1, SAIDA_1, SAIDA_1_2, SAIDA_1_3, SAIDA_1_4, SAIDA_1_5, SAIDA_1_6, SAIDA_1_7, SAIDA_1_8);
  or or_3 (C2, SAIDA_2, SAIDA_2_2, SAIDA_2_3, SAIDA_2_4, SAIDA_2_5, SAIDA_2_6, SAIDA_2_7, SAIDA_2_8);
  or or_4 (C3, SAIDA_3, SAIDA_3_2, SAIDA_3_3, SAIDA_3_4, SAIDA_3_5, SAIDA_3_6, SAIDA_3_7, SAIDA_3_8);
  or or_5 (C4, SAIDA_4, SAIDA_4_2, SAIDA_4_3, SAIDA_4_4, SAIDA_4_5, SAIDA_4_6, SAIDA_4_7, SAIDA_4_8);
  or or_6 (C5, SAIDA_5, SAIDA_5_2, SAIDA_5_3, SAIDA_5_4, SAIDA_5_5, SAIDA_5_6, SAIDA_5_7, SAIDA_5_8);
  or or_7 (C6, SAIDA_6, SAIDA_6_2, SAIDA_6_3, SAIDA_6_4, SAIDA_6_5, SAIDA_6_6, SAIDA_6_7, SAIDA_6_8);
  or or_8 (C7, SAIDA_7, SAIDA_7_2, SAIDA_7_3, SAIDA_7_4, SAIDA_7_5, SAIDA_7_6, SAIDA_7_7, SAIDA_7_8);
endmodule
